// Logisim project laba1.circ as structural Verilog: 44 circuits, main circuit halfsubstracter
module _8_bit_substracter (
  input  [7:0] in_1,
  input  [7:0] in_2,
  output [7:0] out_3,
  output out_4
);

  wire subtracter_1_out_5, subtracter_2_out_5, subtracter_3_out_5, subtracter_4_out_5, subtracter_5_out_5,
       subtracter_6_out_5, subtracter_7_out_5;

  subtracter subtracter_1 (.in_1(in_1[0]), .in_2(in_2[0]), .in_3(1'b0), .out_4(out_3[0]), .out_5(subtracter_1_out_5));
  subtracter subtracter_2 (
    .in_1(in_1[1]), .in_2(in_2[1]), .in_3(subtracter_1_out_5), .out_4(out_3[1]), .out_5(subtracter_2_out_5));
  subtracter subtracter_3 (
    .in_1(in_1[2]), .in_2(in_2[2]), .in_3(subtracter_2_out_5), .out_4(out_3[2]), .out_5(subtracter_3_out_5));
  subtracter subtracter_4 (
    .in_1(in_1[3]), .in_2(in_2[3]), .in_3(subtracter_3_out_5), .out_4(out_3[3]), .out_5(subtracter_4_out_5));
  subtracter subtracter_5 (
    .in_1(in_1[4]), .in_2(in_2[4]), .in_3(subtracter_4_out_5), .out_4(out_3[4]), .out_5(subtracter_5_out_5));
  subtracter subtracter_6 (
    .in_1(in_1[5]), .in_2(in_2[5]), .in_3(subtracter_5_out_5), .out_4(out_3[5]), .out_5(subtracter_6_out_5));
  subtracter subtracter_7 (
    .in_1(in_1[6]), .in_2(in_2[6]), .in_3(subtracter_6_out_5), .out_4(out_3[6]), .out_5(subtracter_7_out_5));
  subtracter subtracter_8 (.in_1(in_1[7]), .in_2(in_2[7]), .in_3(subtracter_7_out_5), .out_4(out_3[7]), .out_5(out_4));
endmodule

module subtracter (
  input  in_1,
  input  in_2,
  input  in_3,
  output out_4,
  output out_5
);

  wire halfsubstracter_1_out_3, halfsubstracter_1_out_4, halfsubstracter_2_out_4;

  halfsubstracter halfsubstracter_1 (
    .in_1(in_1), .in_2(in_2), .out_3(halfsubstracter_1_out_3), .out_4(halfsubstracter_1_out_4));
  halfsubstracter halfsubstracter_2 (
    .in_1(halfsubstracter_1_out_3), .in_2(in_3), .out_3(out_4), .out_4(halfsubstracter_2_out_4));
  or or_1 (out_5, halfsubstracter_2_out_4, halfsubstracter_1_out_4);
endmodule

module halfsubstracter (
  input  in_1,
  input  in_2,
  output out_3,
  output out_4
);

  wire not_1_out;

  not not_1 (not_1_out, in_1);
  xor xor_1 (out_3, in_1, in_2);
  and and_1 (out_4, not_1_out, in_2);
endmodule

module _8_bit_adder (
  input  [7:0] in_1,
  input  [7:0] in_2,
  output [7:0] out_3,
  output out_4
);

  wire adder_1_out_5, adder_2_out_5, adder_3_out_5, adder_4_out_5, adder_5_out_5, adder_6_out_5,
       adder_7_out_5;

  adder adder_1 (.in_1(in_1[0]), .in_2(in_2[0]), .in_3(1'b1), .out_4(out_3[0]), .out_5(adder_1_out_5));
  adder adder_2 (.in_1(in_1[1]), .in_2(in_2[1]), .in_3(adder_1_out_5), .out_4(out_3[1]), .out_5(adder_2_out_5));
  adder adder_3 (.in_1(in_1[2]), .in_2(in_2[2]), .in_3(adder_2_out_5), .out_4(out_3[2]), .out_5(adder_3_out_5));
  adder adder_4 (.in_1(in_1[3]), .in_2(in_2[3]), .in_3(adder_3_out_5), .out_4(out_3[3]), .out_5(adder_4_out_5));
  adder adder_5 (.in_1(in_1[4]), .in_2(in_2[4]), .in_3(adder_4_out_5), .out_4(out_3[4]), .out_5(adder_5_out_5));
  adder adder_6 (.in_1(in_1[5]), .in_2(in_2[5]), .in_3(adder_5_out_5), .out_4(out_3[5]), .out_5(adder_6_out_5));
  adder adder_7 (.in_1(in_1[6]), .in_2(in_2[6]), .in_3(adder_6_out_5), .out_4(out_3[6]), .out_5(adder_7_out_5));
  adder adder_8 (.in_1(in_1[7]), .in_2(in_2[7]), .in_3(adder_7_out_5), .out_4(out_3[7]), .out_5(out_4));
endmodule

module adder (
  input  in_1,
  input  in_2,
  input  in_3,
  output out_4,
  output out_5
);

  wire halfadder_1_out_3, halfadder_1_out_4, halfadder_2_out_4;

  halfadder halfadder_1 (.in_1(in_2), .in_2(in_3), .out_3(halfadder_1_out_3), .out_4(halfadder_1_out_4));
  halfadder halfadder_2 (.in_1(in_1), .in_2(halfadder_1_out_3), .out_3(out_4), .out_4(halfadder_2_out_4));
  or or_1 (out_5, halfadder_2_out_4, halfadder_1_out_4);
endmodule

module halfadder (
  input  in_1,
  input  in_2,
  output out_3,
  output out_4
);

  xor xor_1 (out_3, in_1, in_2);
  and and_1 (out_4, in_1, in_2);
endmodule

module multiplyer (
  input  [7:0] in_1,
  input  [7:0] in_2,
  output [7:0] out_3,
  output [7:0] out_4
);

  wire adder_1_out_4, adder_2_out_4, adder_3_out_4, adder_4_out_4, adder_5_out_4, adder_6_out_4,
       adder_8_out_4, adder_8_out_5, adder_9_out_4, adder_9_out_5, adder_10_out_4, adder_10_out_5,
       adder_11_out_4, adder_11_out_5, adder_12_out_4, adder_12_out_5, adder_13_out_4, adder_13_out_5,
       adder_14_out_5, adder_15_out_4, adder_15_out_5, adder_16_out_4, adder_16_out_5, adder_17_out_4,
       adder_17_out_5, adder_18_out_4, adder_18_out_5, adder_19_out_4, adder_19_out_5, adder_20_out_4,
       adder_20_out_5, adder_21_out_5, adder_22_out_4, adder_22_out_5, adder_23_out_4, adder_23_out_5,
       adder_24_out_4, adder_24_out_5, adder_25_out_4, adder_25_out_5, adder_26_out_4, adder_26_out_5,
       adder_27_out_4, adder_27_out_5, adder_28_out_5, adder_29_out_4, adder_29_out_5, adder_30_out_4,
       adder_30_out_5, adder_31_out_4, adder_31_out_5, adder_32_out_4, adder_32_out_5, adder_33_out_4,
       adder_33_out_5, adder_34_out_4, adder_34_out_5, adder_35_out_5, adder_36_out_4, adder_36_out_5,
       adder_37_out_4, adder_37_out_5, adder_38_out_4, adder_38_out_5, adder_39_out_4, adder_39_out_5,
       adder_40_out_4, adder_40_out_5, adder_41_out_4, adder_41_out_5, adder_42_out_5, adder_43_out_4,
       adder_43_out_5, adder_44_out_4, adder_44_out_5, adder_45_out_4, adder_45_out_5, adder_46_out_4,
       adder_46_out_5, adder_47_out_4, adder_47_out_5, adder_48_out_4, adder_48_out_5, adder_49_out_5,
       adder_50_out_5, adder_51_out_5, adder_52_out_5, adder_53_out_5, adder_54_out_5, adder_55_out_5,
       adder_56_out_5, and_1_out, and_2_out, and_3_out, and_4_out, and_5_out, and_6_out, and_7_out,
       and_8_out, and_9_out, and_10_out, and_11_out, and_12_out, and_13_out, and_14_out, and_15_out,
       and_16_out, and_17_out, and_18_out, and_19_out, and_20_out, and_21_out, and_22_out, and_23_out,
       and_24_out, and_25_out, and_26_out, and_27_out, and_28_out, and_29_out, and_30_out, and_31_out,
       and_32_out, and_33_out, and_34_out, and_35_out, and_36_out, and_37_out, and_38_out, and_39_out,
       and_40_out, and_41_out, and_42_out, and_43_out, and_44_out, and_45_out, and_46_out, and_47_out,
       and_48_out, and_49_out, and_50_out, and_51_out, and_52_out, and_53_out, and_54_out, and_55_out,
       and_56_out, and_57_out, and_58_out, and_59_out, and_60_out, and_61_out, and_63_out, and_64_out;

  adder adder_1 (.in_1(and_1_out), .in_2(1'b0), .in_3(adder_8_out_5), .out_4(adder_1_out_4));  // open: out_5
  adder adder_2 (.in_1(and_2_out), .in_2(1'b0), .in_3(adder_9_out_5), .out_4(adder_2_out_4));  // open: out_5
  adder adder_3 (.in_1(and_3_out), .in_2(1'b0), .in_3(adder_10_out_5), .out_4(adder_3_out_4));  // open: out_5
  adder adder_4 (.in_1(and_4_out), .in_2(1'b0), .in_3(adder_11_out_5), .out_4(adder_4_out_4));  // open: out_5
  adder adder_5 (.in_1(and_5_out), .in_2(1'b0), .in_3(adder_12_out_5), .out_4(adder_5_out_4));  // open: out_5
  adder adder_6 (.in_1(and_6_out), .in_2(1'b0), .in_3(adder_13_out_5), .out_4(adder_6_out_4));  // open: out_5
  adder adder_7 (.in_1(and_7_out), .in_2(1'b0), .in_3(adder_14_out_5), .out_4(out_4[6]), .out_5(out_4[7]));
  and and_1 (and_1_out, in_1[7], in_2[1]);
  adder adder_8 (
    .in_1(and_8_out), .in_2(and_9_out), .in_3(adder_15_out_5), .out_4(adder_8_out_4), .out_5(adder_8_out_5));
  and and_2 (and_2_out, in_2[2], in_1[7]);
  adder adder_9 (
    .in_1(and_10_out), .in_2(adder_1_out_4), .in_3(adder_16_out_5), .out_4(adder_9_out_4),
    .out_5(adder_9_out_5));
  and and_3 (and_3_out, in_2[3], in_1[7]);
  adder adder_10 (
    .in_1(and_11_out), .in_2(adder_2_out_4), .in_3(adder_17_out_5), .out_4(adder_10_out_4),
    .out_5(adder_10_out_5));
  and and_4 (and_4_out, in_2[4], in_1[7]);
  adder adder_11 (
    .in_1(and_12_out), .in_2(adder_3_out_4), .in_3(adder_18_out_5), .out_4(adder_11_out_4),
    .out_5(adder_11_out_5));
  and and_5 (and_5_out, in_2[5], in_1[7]);
  adder adder_12 (
    .in_1(and_13_out), .in_2(adder_4_out_4), .in_3(adder_19_out_5), .out_4(adder_12_out_4),
    .out_5(adder_12_out_5));
  and and_6 (and_6_out, in_2[6], in_1[7]);
  adder adder_13 (
    .in_1(and_14_out), .in_2(adder_5_out_4), .in_3(adder_20_out_5), .out_4(adder_13_out_4),
    .out_5(adder_13_out_5));
  and and_7 (and_7_out, in_2[7], in_1[7]);
  adder adder_14 (
    .in_1(and_15_out), .in_2(adder_6_out_4), .in_3(adder_21_out_5), .out_4(out_4[5]), .out_5(adder_14_out_5));
  and and_8 (and_8_out, in_1[7], in_2[0]);
  and and_9 (and_9_out, in_1[6], in_2[1]);
  adder adder_15 (
    .in_1(and_16_out), .in_2(and_17_out), .in_3(adder_22_out_5), .out_4(adder_15_out_4),
    .out_5(adder_15_out_5));
  and and_10 (and_10_out, in_2[2], in_1[6]);
  adder adder_16 (
    .in_1(and_18_out), .in_2(adder_8_out_4), .in_3(adder_23_out_5), .out_4(adder_16_out_4),
    .out_5(adder_16_out_5));
  and and_11 (and_11_out, in_2[3], in_1[6]);
  adder adder_17 (
    .in_1(and_21_out), .in_2(adder_9_out_4), .in_3(adder_24_out_5), .out_4(adder_17_out_4),
    .out_5(adder_17_out_5));
  and and_12 (and_12_out, in_2[4], in_1[6]);
  adder adder_18 (
    .in_1(and_22_out), .in_2(adder_10_out_4), .in_3(adder_25_out_5), .out_4(adder_18_out_4),
    .out_5(adder_18_out_5));
  and and_13 (and_13_out, in_2[5], in_1[6]);
  adder adder_19 (
    .in_1(and_24_out), .in_2(adder_11_out_4), .in_3(adder_26_out_5), .out_4(adder_19_out_4),
    .out_5(adder_19_out_5));
  and and_14 (and_14_out, in_2[6], in_1[6]);
  adder adder_20 (
    .in_1(and_27_out), .in_2(adder_12_out_4), .in_3(adder_27_out_5), .out_4(adder_20_out_4),
    .out_5(adder_20_out_5));
  and and_15 (and_15_out, in_2[7], in_1[6]);
  adder adder_21 (
    .in_1(and_28_out), .in_2(adder_13_out_4), .in_3(adder_28_out_5), .out_4(out_4[4]), .out_5(adder_21_out_5));
  and and_16 (and_16_out, in_1[6], in_2[0]);
  and and_17 (and_17_out, in_1[5], in_2[1]);
  adder adder_22 (
    .in_1(and_30_out), .in_2(and_33_out), .in_3(adder_29_out_5), .out_4(adder_22_out_4),
    .out_5(adder_22_out_5));
  and and_18 (and_18_out, in_2[2], in_1[5]);
  and and_19 (and_19_out, in_2[2], in_1[4]);
  adder adder_23 (
    .in_1(and_19_out), .in_2(adder_15_out_4), .in_3(adder_30_out_5), .out_4(adder_23_out_4),
    .out_5(adder_23_out_5));
  and and_20 (and_20_out, in_2[3], in_1[4]);
  and and_21 (and_21_out, in_2[3], in_1[5]);
  adder adder_24 (
    .in_1(and_20_out), .in_2(adder_16_out_4), .in_3(adder_31_out_5), .out_4(adder_24_out_4),
    .out_5(adder_24_out_5));
  and and_22 (and_22_out, in_2[4], in_1[5]);
  and and_23 (and_23_out, in_2[4], in_1[4]);
  adder adder_25 (
    .in_1(and_23_out), .in_2(adder_17_out_4), .in_3(adder_32_out_5), .out_4(adder_25_out_4),
    .out_5(adder_25_out_5));
  and and_24 (and_24_out, in_2[5], in_1[5]);
  and and_25 (and_25_out, in_2[5], in_1[4]);
  adder adder_26 (
    .in_1(and_25_out), .in_2(adder_18_out_4), .in_3(adder_33_out_5), .out_4(adder_26_out_4),
    .out_5(adder_26_out_5));
  and and_26 (and_26_out, in_2[6], in_1[4]);
  and and_27 (and_27_out, in_2[6], in_1[5]);
  adder adder_27 (
    .in_1(and_26_out), .in_2(adder_19_out_4), .in_3(adder_34_out_5), .out_4(adder_27_out_4),
    .out_5(adder_27_out_5));
  and and_28 (and_28_out, in_2[7], in_1[5]);
  and and_29 (and_29_out, in_2[7], in_1[4]);
  adder adder_28 (
    .in_1(and_29_out), .in_2(adder_20_out_4), .in_3(adder_35_out_5), .out_4(out_4[3]), .out_5(adder_28_out_5));
  and and_30 (and_30_out, in_1[5], in_2[0]);
  and and_31 (and_31_out, in_1[4], in_2[0]);
  and and_32 (and_32_out, in_1[3], in_2[1]);
  and and_33 (and_33_out, in_1[4], in_2[1]);
  adder adder_29 (
    .in_1(and_31_out), .in_2(and_32_out), .in_3(adder_36_out_5), .out_4(adder_29_out_4),
    .out_5(adder_29_out_5));
  and and_34 (and_34_out, in_2[2], in_1[3]);
  adder adder_30 (
    .in_1(and_34_out), .in_2(adder_22_out_4), .in_3(adder_37_out_5), .out_4(adder_30_out_4),
    .out_5(adder_30_out_5));
  and and_35 (and_35_out, in_2[3], in_1[3]);
  adder adder_31 (
    .in_1(and_35_out), .in_2(adder_23_out_4), .in_3(adder_38_out_5), .out_4(adder_31_out_4),
    .out_5(adder_31_out_5));
  and and_36 (and_36_out, in_2[4], in_1[3]);
  adder adder_32 (
    .in_1(and_36_out), .in_2(adder_24_out_4), .in_3(adder_39_out_5), .out_4(adder_32_out_4),
    .out_5(adder_32_out_5));
  and and_37 (and_37_out, in_2[5], in_1[3]);
  adder adder_33 (
    .in_1(and_37_out), .in_2(adder_25_out_4), .in_3(adder_40_out_5), .out_4(adder_33_out_4),
    .out_5(adder_33_out_5));
  and and_38 (and_38_out, in_2[6], in_1[3]);
  adder adder_34 (
    .in_1(and_38_out), .in_2(adder_26_out_4), .in_3(adder_41_out_5), .out_4(adder_34_out_4),
    .out_5(adder_34_out_5));
  and and_39 (and_39_out, in_2[7], in_1[3]);
  adder adder_35 (
    .in_1(and_39_out), .in_2(adder_27_out_4), .in_3(adder_42_out_5), .out_4(out_4[2]), .out_5(adder_35_out_5));
  and and_40 (and_40_out, in_1[3], in_2[0]);
  and and_41 (and_41_out, in_1[2], in_2[1]);
  adder adder_36 (
    .in_1(and_40_out), .in_2(and_41_out), .in_3(adder_43_out_5), .out_4(adder_36_out_4),
    .out_5(adder_36_out_5));
  and and_42 (and_42_out, in_2[2], in_1[2]);
  adder adder_37 (
    .in_1(and_42_out), .in_2(adder_29_out_4), .in_3(adder_44_out_5), .out_4(adder_37_out_4),
    .out_5(adder_37_out_5));
  and and_43 (and_43_out, in_2[3], in_1[2]);
  adder adder_38 (
    .in_1(and_43_out), .in_2(adder_30_out_4), .in_3(adder_45_out_5), .out_4(adder_38_out_4),
    .out_5(adder_38_out_5));
  and and_44 (and_44_out, in_2[4], in_1[2]);
  adder adder_39 (
    .in_1(and_44_out), .in_2(adder_31_out_4), .in_3(adder_46_out_5), .out_4(adder_39_out_4),
    .out_5(adder_39_out_5));
  and and_45 (and_45_out, in_2[5], in_1[2]);
  adder adder_40 (
    .in_1(and_45_out), .in_2(adder_32_out_4), .in_3(adder_47_out_5), .out_4(adder_40_out_4),
    .out_5(adder_40_out_5));
  and and_46 (and_46_out, in_2[6], in_1[2]);
  adder adder_41 (
    .in_1(and_46_out), .in_2(adder_33_out_4), .in_3(adder_48_out_5), .out_4(adder_41_out_4),
    .out_5(adder_41_out_5));
  and and_47 (and_47_out, in_2[7], in_1[2]);
  adder adder_42 (
    .in_1(and_47_out), .in_2(adder_34_out_4), .in_3(adder_49_out_5), .out_4(out_4[1]), .out_5(adder_42_out_5));
  and and_48 (and_48_out, in_1[2], in_2[0]);
  and and_49 (and_49_out, in_1[1], in_2[1]);
  adder adder_43 (
    .in_1(and_48_out), .in_2(and_49_out), .in_3(adder_50_out_5), .out_4(adder_43_out_4),
    .out_5(adder_43_out_5));
  and and_50 (and_50_out, in_2[2], in_1[0]);
  and and_51 (and_51_out, in_2[2], in_1[1]);
  adder adder_44 (
    .in_1(and_51_out), .in_2(adder_36_out_4), .in_3(adder_51_out_5), .out_4(adder_44_out_4),
    .out_5(adder_44_out_5));
  and and_52 (and_52_out, in_2[3], in_1[1]);
  and and_53 (and_53_out, in_2[3], in_1[0]);
  adder adder_45 (
    .in_1(and_52_out), .in_2(adder_37_out_4), .in_3(adder_52_out_5), .out_4(adder_45_out_4),
    .out_5(adder_45_out_5));
  and and_54 (and_54_out, in_2[4], in_1[1]);
  and and_55 (and_55_out, in_2[4], in_1[0]);
  adder adder_46 (
    .in_1(and_54_out), .in_2(adder_38_out_4), .in_3(adder_53_out_5), .out_4(adder_46_out_4),
    .out_5(adder_46_out_5));
  and and_56 (and_56_out, in_2[5], in_1[0]);
  and and_57 (and_57_out, in_2[5], in_1[1]);
  adder adder_47 (
    .in_1(and_57_out), .in_2(adder_39_out_4), .in_3(adder_54_out_5), .out_4(adder_47_out_4),
    .out_5(adder_47_out_5));
  and and_58 (and_58_out, in_2[6], in_1[0]);
  and and_59 (and_59_out, in_2[6], in_1[1]);
  adder adder_48 (
    .in_1(and_59_out), .in_2(adder_40_out_4), .in_3(adder_55_out_5), .out_4(adder_48_out_4),
    .out_5(adder_48_out_5));
  and and_60 (and_60_out, in_2[7], in_1[0]);
  and and_61 (and_61_out, in_2[7], in_1[1]);
  adder adder_49 (
    .in_1(and_61_out), .in_2(adder_41_out_4), .in_3(adder_56_out_5), .out_4(out_4[0]), .out_5(adder_49_out_5));
  and and_62 (out_3[0], in_1[0], in_2[0]);
  and and_63 (and_63_out, in_1[1], in_2[0]);
  and and_64 (and_64_out, in_1[0], in_2[1]);
  adder adder_50 (.in_1(and_63_out), .in_2(and_64_out), .in_3(1'b0), .out_4(out_3[1]), .out_5(adder_50_out_5));
  adder adder_51 (.in_1(and_50_out), .in_2(adder_43_out_4), .in_3(1'b0), .out_4(out_3[2]), .out_5(adder_51_out_5));
  adder adder_52 (.in_1(and_53_out), .in_2(adder_44_out_4), .in_3(1'b0), .out_4(out_3[3]), .out_5(adder_52_out_5));
  adder adder_53 (.in_1(and_55_out), .in_2(adder_45_out_4), .in_3(1'b0), .out_4(out_3[4]), .out_5(adder_53_out_5));
  adder adder_54 (.in_1(and_56_out), .in_2(adder_46_out_4), .in_3(1'b0), .out_4(out_3[5]), .out_5(adder_54_out_5));
  adder adder_55 (.in_1(and_58_out), .in_2(adder_47_out_4), .in_3(1'b0), .out_4(out_3[6]), .out_5(adder_55_out_5));
  adder adder_56 (.in_1(and_60_out), .in_2(adder_48_out_4), .in_3(1'b0), .out_4(out_3[7]), .out_5(adder_56_out_5));

  // Other names for the same wires on the sheet: _8 = in_1[0]; _7 = in_1[1]; _6 = in_1[2]; _5 = in_1[3]; _4 = in_1[4];
  //   _3 = in_1[5]; _2 = in_1[6]; _1 = in_1[7]
endmodule

module _8_bit_and (
  input  [7:0] in_1,
  input  [7:0] in_2,
  output [7:0] out_3
);

  and and_1 (out_3[0], in_1[0], in_2[0]);
  and and_2 (out_3[1], in_1[1], in_2[1]);
  and and_3 (out_3[2], in_1[2], in_2[2]);
  and and_4 (out_3[3], in_1[3], in_2[3]);
  and and_5 (out_3[4], in_1[4], in_2[4]);
  and and_6 (out_3[5], in_1[5], in_2[5]);
  and and_7 (out_3[6], in_1[6], in_2[6]);
  and and_8 (out_3[7], in_1[7], in_2[7]);
endmodule

module _8_bit_logic_and (
  input  [7:0] in_1,
  input  [7:0] in_2,
  output out_3
);

  wire or_1_out, or_2_out, or_3_out, or_4_out, or_5_out, or_6_out, or_7_out, or_8_out, or_9_out, or_10_out,
       or_11_out, or_12_out, or_13_out, or_14_out;

  or or_1 (or_1_out, in_1[0], or_2_out);
  or or_2 (or_2_out, in_1[1], or_3_out);
  or or_3 (or_3_out, in_1[2], or_4_out);
  or or_4 (or_4_out, in_1[3], or_5_out);
  or or_5 (or_5_out, in_1[4], or_6_out);
  or or_6 (or_6_out, in_1[5], or_7_out);
  or or_7 (or_7_out, in_1[6], in_1[7]);
  or or_8 (or_8_out, in_2[0], or_9_out);
  or or_9 (or_9_out, in_2[1], or_10_out);
  or or_10 (or_10_out, in_2[2], or_11_out);
  or or_11 (or_11_out, in_2[3], or_12_out);
  or or_12 (or_12_out, in_2[4], or_13_out);
  or or_13 (or_13_out, in_2[5], or_14_out);
  or or_14 (or_14_out, in_2[6], in_2[7]);
  and and_1 (out_3, or_1_out, or_8_out);
endmodule

module _8_bit_or (
  input  [7:0] in_1,
  input  [7:0] in_2,
  output [7:0] out_3
);

  or or_1 (out_3[0], in_1[0], in_2[0]);
  or or_2 (out_3[1], in_1[1], in_2[1]);
  or or_3 (out_3[2], in_1[2], in_2[2]);
  or or_4 (out_3[3], in_1[3], in_2[3]);
  or or_5 (out_3[4], in_1[4], in_2[4]);
  or or_6 (out_3[5], in_1[5], in_2[5]);
  or or_7 (out_3[6], in_1[6], in_2[6]);
  or or_8 (out_3[7], in_1[7], in_2[7]);
endmodule

module _8_bit_logic_or (
  input  [7:0] in_1,
  input  [7:0] in_2,
  output out_3
);

  wire or_1_out, or_2_out, or_3_out, or_4_out, or_5_out, or_6_out, or_7_out, or_8_out, or_9_out, or_10_out,
       or_11_out, or_12_out, or_13_out, or_14_out;

  or or_1 (or_1_out, in_1[0], or_2_out);
  or or_2 (or_2_out, in_1[1], or_3_out);
  or or_3 (or_3_out, in_1[2], or_4_out);
  or or_4 (or_4_out, in_1[3], or_5_out);
  or or_5 (or_5_out, in_1[4], or_6_out);
  or or_6 (or_6_out, in_1[5], or_7_out);
  or or_7 (or_7_out, in_1[6], in_1[7]);
  or or_8 (or_8_out, in_2[0], or_9_out);
  or or_9 (or_9_out, in_2[1], or_10_out);
  or or_10 (or_10_out, in_2[2], or_11_out);
  or or_11 (or_11_out, in_2[3], or_12_out);
  or or_12 (or_12_out, in_2[4], or_13_out);
  or or_13 (or_13_out, in_2[5], or_14_out);
  or or_14 (or_14_out, in_2[6], in_2[7]);
  or or_15 (out_3, or_1_out, or_8_out);
endmodule

module _8_bit_xor (
  input  [7:0] in_1,
  input  [7:0] in_2,
  output [7:0] out_3
);

  xor xor_1 (out_3[0], in_1[0], in_2[0]);
  xor xor_2 (out_3[1], in_1[1], in_2[1]);
  xor xor_3 (out_3[2], in_1[2], in_2[2]);
  xor xor_4 (out_3[3], in_1[3], in_2[3]);
  xor xor_5 (out_3[4], in_1[4], in_2[4]);
  xor xor_6 (out_3[5], in_1[5], in_2[5]);
  xor xor_7 (out_3[6], in_1[6], in_2[6]);
  xor xor_8 (out_3[7], in_1[7], in_2[7]);
endmodule

module _8_bit_logic_xor (
  input  [7:0] in_1,
  input  [7:0] in_2,
  output out_3
);

  wire or_1_out, or_2_out, or_3_out, or_4_out, or_5_out, or_6_out, or_7_out, or_8_out, or_9_out, or_10_out,
       or_11_out, or_12_out, or_13_out, or_14_out;

  or or_1 (or_1_out, in_1[0], or_2_out);
  or or_2 (or_2_out, in_1[1], or_3_out);
  or or_3 (or_3_out, in_1[2], or_4_out);
  or or_4 (or_4_out, in_1[3], or_5_out);
  or or_5 (or_5_out, in_1[4], or_6_out);
  or or_6 (or_6_out, in_1[5], or_7_out);
  or or_7 (or_7_out, in_1[6], in_1[7]);
  or or_8 (or_8_out, in_2[0], or_9_out);
  or or_9 (or_9_out, in_2[1], or_10_out);
  or or_10 (or_10_out, in_2[2], or_11_out);
  or or_11 (or_11_out, in_2[3], or_12_out);
  or or_12 (or_12_out, in_2[4], or_13_out);
  or or_13 (or_13_out, in_2[5], or_14_out);
  or or_14 (or_14_out, in_2[6], in_2[7]);
  xor xor_1 (out_3, or_1_out, or_8_out);
endmodule

module _8_it_not (
  input  [7:0] in_1,
  output [7:0] out_2
);

  not not_1 (out_2[0], in_1[0]);
  not not_2 (out_2[1], in_1[1]);
  not not_3 (out_2[2], in_1[2]);
  not not_4 (out_2[3], in_1[3]);
  not not_5 (out_2[4], in_1[4]);
  not not_6 (out_2[5], in_1[5]);
  not not_7 (out_2[6], in_1[6]);
  not not_8 (out_2[7], in_1[7]);
endmodule

module _8_bit_llogic_not (
  input  [7:0] in_1,
  output out_2
);

  wire or_1_out, or_2_out, or_3_out, or_4_out, or_5_out, or_6_out, or_7_out;

  or or_1 (or_1_out, in_1[0], or_2_out);
  or or_2 (or_2_out, in_1[1], or_3_out);
  or or_3 (or_3_out, in_1[2], or_4_out);
  or or_4 (or_4_out, in_1[3], or_5_out);
  or or_5 (or_5_out, in_1[4], or_6_out);
  or or_6 (or_6_out, in_1[5], or_7_out);
  or or_7 (or_7_out, in_1[6], in_1[7]);
  not not_1 (out_2, or_1_out);
endmodule

module Less (
  input  in_1,
  input  in_2,
  output out_3
);

  wire not_1_out;

  not not_1 (not_1_out, in_1);
  and and_1 (out_3, not_1_out, in_2);
endmodule

module not_more (
  input  in_1,
  input  in_2,
  output out_3
);

  wire not_1_out;

  not not_1 (not_1_out, in_2);
  nand nand_1 (out_3, in_1, not_1_out);
endmodule

module less_8_bit_nosign (
  input  [7:0] in_1,
  input  [7:0] in_2,
  output out_3
);

  wire and_1_out, and_2_out, and_3_out, and_4_out, and_5_out, and_6_out, and_7_out, less_1_out_3,
       less_2_out_3, less_3_out_3, less_4_out_3, less_5_out_3, less_6_out_3, less_7_out_3, less_8_out_3,
       not_more_1_out_3, not_more_2_out_3, not_more_3_out_3, not_more_4_out_3, not_more_5_out_3,
       not_more_6_out_3, not_more_7_out_3;

  Less less_1 (.in_1(in_1[7]), .in_2(in_2[7]), .out_3(less_1_out_3));
  Less less_2 (.in_1(in_1[6]), .in_2(in_2[6]), .out_3(less_2_out_3));
  Less less_3 (.in_1(in_1[5]), .in_2(in_2[5]), .out_3(less_3_out_3));
  not_more not_more_1 (.in_1(in_1[7]), .in_2(in_2[7]), .out_3(not_more_1_out_3));
  not_more not_more_2 (.in_1(in_1[6]), .in_2(in_2[6]), .out_3(not_more_2_out_3));
  not_more not_more_3 (.in_1(in_1[5]), .in_2(in_2[5]), .out_3(not_more_3_out_3));
  Less less_4 (.in_1(in_1[4]), .in_2(in_2[4]), .out_3(less_4_out_3));
  not_more not_more_4 (.in_1(in_1[4]), .in_2(in_2[4]), .out_3(not_more_4_out_3));
  Less less_5 (.in_1(in_1[3]), .in_2(in_2[3]), .out_3(less_5_out_3));
  not_more not_more_5 (.in_1(in_1[3]), .in_2(in_2[3]), .out_3(not_more_5_out_3));
  Less less_6 (.in_1(in_1[2]), .in_2(in_2[2]), .out_3(less_6_out_3));
  not_more not_more_6 (.in_1(in_1[2]), .in_2(in_2[2]), .out_3(not_more_6_out_3));
  Less less_7 (.in_1(in_1[1]), .in_2(in_2[1]), .out_3(less_7_out_3));
  not_more not_more_7 (.in_1(in_1[1]), .in_2(in_2[1]), .out_3(not_more_7_out_3));
  Less less_8 (.in_1(in_1[0]), .in_2(in_2[0]), .out_3(less_8_out_3));
  and and_1 (and_1_out, not_more_1_out_3, less_2_out_3);
  and and_2 (and_2_out, not_more_1_out_3, not_more_2_out_3, less_3_out_3);
  and and_3 (and_3_out, not_more_1_out_3, not_more_2_out_3, not_more_3_out_3, less_4_out_3);
  and and_4 (and_4_out, not_more_1_out_3, not_more_2_out_3, not_more_3_out_3, not_more_4_out_3, less_5_out_3);
  and and_5 (and_5_out, not_more_1_out_3, not_more_2_out_3, not_more_3_out_3, not_more_4_out_3, not_more_5_out_3, less_6_out_3);
  and and_6 (and_6_out, not_more_1_out_3, not_more_2_out_3, not_more_3_out_3, not_more_4_out_3, not_more_5_out_3, not_more_6_out_3, less_7_out_3);
  and and_7 (and_7_out, not_more_1_out_3, not_more_2_out_3, not_more_3_out_3, not_more_4_out_3, not_more_5_out_3, not_more_6_out_3, not_more_7_out_3, less_8_out_3);
  or or_1 (out_3, less_1_out_3, and_1_out, and_2_out, and_3_out, and_4_out, and_5_out, and_6_out, and_7_out);
endmodule

module more_8_bit_nosign (
  input  [7:0] in_1,
  input  [7:0] in_2,
  output out_3
);

  less_8_bit_nosign less_8_bit_nosign_1 (.in_1(in_2), .in_2(in_1), .out_3(out_3));
endmodule

module equal_8_bit (
  input  [7:0] in_1,
  input  [7:0] in_2,
  output out_3
);

  wire xnor_1_out, xnor_2_out, xnor_3_out, xnor_4_out, xnor_5_out, xnor_6_out, xnor_7_out, xnor_8_out;

  xnor xnor_1 (xnor_1_out, in_1[7], in_2[7]);
  xnor xnor_2 (xnor_2_out, in_1[5], in_2[5]);
  xnor xnor_3 (xnor_3_out, in_1[6], in_2[6]);
  xnor xnor_4 (xnor_4_out, in_1[4], in_2[4]);
  xnor xnor_5 (xnor_5_out, in_1[3], in_2[3]);
  xnor xnor_6 (xnor_6_out, in_1[1], in_2[1]);
  xnor xnor_7 (xnor_7_out, in_1[2], in_2[2]);
  xnor xnor_8 (xnor_8_out, in_1[0], in_2[0]);
  and and_1 (out_3, xnor_8_out, xnor_6_out, xnor_7_out, xnor_5_out, xnor_4_out, xnor_2_out, xnor_3_out, xnor_1_out);
endmodule

module less_or_equal_8_bit_nosign (
  input  [7:0] in_1,
  input  [7:0] in_2,
  output out_3
);

  wire equal_8_bit_1_out_3, less_8_bit_nosign_1_out_3;

  less_8_bit_nosign less_8_bit_nosign_1 (.in_1(in_1), .in_2(in_2), .out_3(less_8_bit_nosign_1_out_3));
  equal_8_bit equal_8_bit_1 (.in_1(in_1), .in_2(in_2), .out_3(equal_8_bit_1_out_3));
  or or_1 (out_3, less_8_bit_nosign_1_out_3, equal_8_bit_1_out_3);
endmodule

module more_or_equal_8_bit_nosign (
  input  [7:0] in_1,
  input  [7:0] in_2,
  output out_3
);

  wire equal_8_bit_1_out_3, more_8_bit_nosign_1_out_3;

  more_8_bit_nosign more_8_bit_nosign_1 (.in_1(in_1), .in_2(in_2), .out_3(more_8_bit_nosign_1_out_3));
  equal_8_bit equal_8_bit_1 (.in_1(in_1), .in_2(in_2), .out_3(equal_8_bit_1_out_3));
  or or_1 (out_3, more_8_bit_nosign_1_out_3, equal_8_bit_1_out_3);
endmodule

module not_equal_8_bit (
  input  [7:0] in_1,
  input  [7:0] in_2,
  output out_3
);

  wire equal_8_bit_1_out_3;

  equal_8_bit equal_8_bit_1 (.in_1(in_1), .in_2(in_2), .out_3(equal_8_bit_1_out_3));
  not not_1 (out_3, equal_8_bit_1_out_3);
endmodule

module less_7_bit_nosign (
  input  [6:0] in_1,
  input  [6:0] in_2,
  output out_3
);

  wire and_1_out, and_2_out, and_3_out, and_4_out, and_5_out, and_6_out, less_1_out_3, less_2_out_3,
       less_3_out_3, less_4_out_3, less_5_out_3, less_6_out_3, less_7_out_3, not_more_1_out_3,
       not_more_2_out_3, not_more_3_out_3, not_more_4_out_3, not_more_5_out_3, not_more_6_out_3;

  Less less_1 (.in_1(in_1[6]), .in_2(in_2[6]), .out_3(less_1_out_3));
  Less less_2 (.in_1(in_1[5]), .in_2(in_2[5]), .out_3(less_2_out_3));
  Less less_3 (.in_1(in_1[4]), .in_2(in_2[4]), .out_3(less_3_out_3));
  not_more not_more_1 (.in_1(in_1[6]), .in_2(in_2[6]), .out_3(not_more_1_out_3));
  not_more not_more_2 (.in_1(in_1[5]), .in_2(in_2[5]), .out_3(not_more_2_out_3));
  not_more not_more_3 (.in_1(in_1[4]), .in_2(in_2[4]), .out_3(not_more_3_out_3));
  Less less_4 (.in_1(in_1[3]), .in_2(in_2[3]), .out_3(less_4_out_3));
  not_more not_more_4 (.in_1(in_1[3]), .in_2(in_2[3]), .out_3(not_more_4_out_3));
  Less less_5 (.in_1(in_1[2]), .in_2(in_2[2]), .out_3(less_5_out_3));
  not_more not_more_5 (.in_1(in_1[2]), .in_2(in_2[2]), .out_3(not_more_5_out_3));
  Less less_6 (.in_1(in_1[1]), .in_2(in_2[1]), .out_3(less_6_out_3));
  not_more not_more_6 (.in_1(in_1[1]), .in_2(in_2[1]), .out_3(not_more_6_out_3));
  Less less_7 (.in_1(in_1[0]), .in_2(in_2[0]), .out_3(less_7_out_3));
  and and_1 (and_1_out, not_more_1_out_3, less_2_out_3);
  and and_2 (and_2_out, not_more_1_out_3, not_more_2_out_3, less_3_out_3);
  and and_3 (and_3_out, not_more_1_out_3, not_more_2_out_3, not_more_3_out_3, less_4_out_3);
  and and_4 (and_4_out, not_more_1_out_3, not_more_2_out_3, not_more_3_out_3, not_more_4_out_3, less_5_out_3);
  and and_5 (and_5_out, not_more_1_out_3, not_more_2_out_3, not_more_3_out_3, not_more_4_out_3, not_more_5_out_3, less_6_out_3);
  and and_6 (and_6_out, not_more_1_out_3, not_more_2_out_3, not_more_3_out_3, not_more_4_out_3, not_more_5_out_3, not_more_6_out_3, less_7_out_3);
  or or_1 (out_3, less_1_out_3, and_1_out, and_2_out, and_3_out, and_4_out, and_5_out, and_6_out);
endmodule

module more_7_bit_nosign (
  input  [6:0] in_1,
  input  [6:0] in_2,
  output out_3
);

  less_7_bit_nosign less_7_bit_nosign_1 (.in_1(in_2), .in_2(in_1), .out_3(out_3));
endmodule

module less_8_bit_sign (
  input  [7:0] in_1,
  input  [7:0] in_2,
  output out_3
);

  wire and_1_out, and_2_out, and_3_out, less_7_bit_nosign_1_out_3, more_7_bit_nosign_1_out_3, not_1_out,
       not_2_out, not_3_out, not_4_out;

  not not_1 (not_1_out, in_2[7]);
  less_7_bit_nosign less_7_bit_nosign_1 (.in_1(in_1[6:0]), .in_2(in_2[6:0]), .out_3(less_7_bit_nosign_1_out_3));
  more_7_bit_nosign more_7_bit_nosign_1 (.in_1(in_1[6:0]), .in_2(in_2[6:0]), .out_3(more_7_bit_nosign_1_out_3));
  not not_2 (not_2_out, more_7_bit_nosign_1_out_3);
  not not_3 (not_3_out, less_7_bit_nosign_1_out_3);
  and and_1 (and_1_out, in_1[7], not_3_out, more_7_bit_nosign_1_out_3);
  and and_2 (and_2_out, in_1[7], not_1_out, not_4_out);
  not not_4 (not_4_out, more_7_bit_nosign_1_out_3);
  and and_3 (and_3_out, less_7_bit_nosign_1_out_3, not_2_out, not_1_out);
  or or_1 (out_3, and_1_out, and_2_out, and_3_out);
endmodule

module more_8_bit_sign (
  input  [7:0] in_1,
  input  [7:0] in_2,
  output out_3
);

  less_8_bit_sign less_8_bit_sign_1 (.in_1(in_2), .in_2(in_1), .out_3(out_3));
endmodule

module less_or_equal_8_bit_sign (
  input  [7:0] in_1,
  input  [7:0] in_2,
  output out_3
);

  wire equal_8_bit_1_out_3, less_8_bit_sign_1_out_3;

  less_8_bit_sign less_8_bit_sign_1 (.in_1(in_1), .in_2(in_2), .out_3(less_8_bit_sign_1_out_3));
  equal_8_bit equal_8_bit_1 (.in_1(in_1), .in_2(in_2), .out_3(equal_8_bit_1_out_3));
  or or_1 (out_3, less_8_bit_sign_1_out_3, equal_8_bit_1_out_3);
endmodule

module more_or_equal_8_bit_sign (
  input  [7:0] in_1,
  input  [7:0] in_2,
  output out_3
);

  wire equal_8_bit_1_out_3, more_8_bit_sign_1_out_3;

  more_8_bit_sign more_8_bit_sign_1 (.in_1(in_1), .in_2(in_2), .out_3(more_8_bit_sign_1_out_3));
  equal_8_bit equal_8_bit_1 (.in_1(in_1), .in_2(in_2), .out_3(equal_8_bit_1_out_3));
  or or_1 (out_3, more_8_bit_sign_1_out_3, equal_8_bit_1_out_3);
endmodule

module Logic_arifmetic_shift_left (
  input  [2:0] in_1,
  input  [7:0] in_2,
  output [7:0] out_3
);

  wire multiplexer_1_out, multiplexer_2_out, multiplexer_3_out, multiplexer_4_out, multiplexer_5_out,
       multiplexer_6_out, multiplexer_7_out, multiplexer_8_out, multiplexer_9_out, multiplexer_10_out,
       multiplexer_11_out, multiplexer_12_out, multiplexer_13_out, multiplexer_14_out, multiplexer_15_out,
       multiplexer_16_out, not_1_out, not_2_out, not_3_out;

  not not_1 (not_1_out, in_1[2]);
  not not_2 (not_2_out, in_1[1]);
  not not_3 (not_3_out, in_1[0]);
  Multiplexer multiplexer_1 (.in0(1'b0), .in1(in_2[0]), .out(multiplexer_1_out), .sel(not_3_out));  // open: en
  Multiplexer multiplexer_2 (.in0(in_2[0]), .in1(in_2[1]), .out(multiplexer_2_out), .sel(not_3_out));  // open: en
  Multiplexer multiplexer_3 (.in0(in_2[1]), .in1(in_2[2]), .out(multiplexer_3_out), .sel(not_3_out));  // open: en
  Multiplexer multiplexer_4 (.in0(in_2[2]), .in1(in_2[3]), .out(multiplexer_4_out), .sel(not_3_out));  // open: en
  Multiplexer multiplexer_5 (.in0(in_2[3]), .in1(in_2[4]), .out(multiplexer_5_out), .sel(not_3_out));  // open: en
  Multiplexer multiplexer_6 (.in0(in_2[4]), .in1(in_2[5]), .out(multiplexer_6_out), .sel(not_3_out));  // open: en
  Multiplexer multiplexer_7 (.in0(in_2[5]), .in1(in_2[6]), .out(multiplexer_7_out), .sel(not_3_out));  // open: en
  Multiplexer multiplexer_8 (.in0(in_2[6]), .in1(in_2[7]), .out(multiplexer_8_out), .sel(not_3_out));  // open: en
  Multiplexer multiplexer_9 (
    .in0(1'b0), .in1(multiplexer_1_out), .out(multiplexer_9_out), .sel(not_2_out));  // open: en
  Multiplexer multiplexer_10 (
    .in0(1'b0), .in1(multiplexer_2_out), .out(multiplexer_10_out), .sel(not_2_out));  // open: en
  Multiplexer multiplexer_11 (
    .in0(multiplexer_1_out), .in1(multiplexer_3_out), .out(multiplexer_11_out), .sel(not_2_out));  // open: en
  Multiplexer multiplexer_12 (
    .in0(multiplexer_2_out), .in1(multiplexer_4_out), .out(multiplexer_12_out), .sel(not_2_out));  // open: en
  Multiplexer multiplexer_13 (
    .in0(multiplexer_3_out), .in1(multiplexer_5_out), .out(multiplexer_13_out), .sel(not_2_out));  // open: en
  Multiplexer multiplexer_14 (
    .in0(multiplexer_4_out), .in1(multiplexer_6_out), .out(multiplexer_14_out), .sel(not_2_out));  // open: en
  Multiplexer multiplexer_15 (
    .in0(multiplexer_5_out), .in1(multiplexer_7_out), .out(multiplexer_15_out), .sel(not_2_out));  // open: en
  Multiplexer multiplexer_16 (
    .in0(multiplexer_6_out), .in1(multiplexer_8_out), .out(multiplexer_16_out), .sel(not_2_out));  // open: en
  Multiplexer multiplexer_17 (.in0(1'b0), .in1(multiplexer_9_out), .out(out_3[0]), .sel(not_1_out));  // open: en
  Multiplexer multiplexer_18 (.in0(1'b0), .in1(multiplexer_10_out), .out(out_3[1]), .sel(not_1_out));  // open: en
  Multiplexer multiplexer_19 (.in0(1'b0), .in1(multiplexer_11_out), .out(out_3[2]), .sel(not_1_out));  // open: en
  Multiplexer multiplexer_20 (.in0(1'b0), .in1(multiplexer_12_out), .out(out_3[3]), .sel(not_1_out));  // open: en
  Multiplexer multiplexer_21 (
    .in0(multiplexer_9_out), .in1(multiplexer_13_out), .out(out_3[4]), .sel(not_1_out));  // open: en
  Multiplexer multiplexer_22 (
    .in0(multiplexer_10_out), .in1(multiplexer_14_out), .out(out_3[5]), .sel(not_1_out));  // open: en
  Multiplexer multiplexer_23 (
    .in0(multiplexer_11_out), .in1(multiplexer_15_out), .out(out_3[6]), .sel(not_1_out));  // open: en
  Multiplexer multiplexer_24 (
    .in0(multiplexer_12_out), .in1(multiplexer_16_out), .out(out_3[7]), .sel(not_1_out));  // open: en
endmodule

module logic_shift_right (
  input  [2:0] in_1,
  input  [7:0] in_2,
  output [7:0] out_3
);

  wire multiplexer_1_out, multiplexer_2_out, multiplexer_3_out, multiplexer_4_out, multiplexer_5_out,
       multiplexer_6_out, multiplexer_7_out, multiplexer_8_out, multiplexer_9_out, multiplexer_10_out,
       multiplexer_11_out, multiplexer_12_out, multiplexer_13_out, multiplexer_14_out, multiplexer_15_out,
       multiplexer_16_out, not_1_out, not_2_out, not_3_out;

  not not_1 (not_1_out, in_1[2]);
  not not_2 (not_2_out, in_1[1]);
  not not_3 (not_3_out, in_1[0]);
  Multiplexer multiplexer_1 (.in0(1'b0), .in1(in_2[7]), .out(multiplexer_1_out), .sel(not_3_out));  // open: en
  Multiplexer multiplexer_2 (.in0(in_2[7]), .in1(in_2[6]), .out(multiplexer_2_out), .sel(not_3_out));  // open: en
  Multiplexer multiplexer_3 (.in0(in_2[6]), .in1(in_2[5]), .out(multiplexer_3_out), .sel(not_3_out));  // open: en
  Multiplexer multiplexer_4 (.in0(in_2[5]), .in1(in_2[4]), .out(multiplexer_4_out), .sel(not_3_out));  // open: en
  Multiplexer multiplexer_5 (.in0(in_2[4]), .in1(in_2[3]), .out(multiplexer_5_out), .sel(not_3_out));  // open: en
  Multiplexer multiplexer_6 (.in0(in_2[3]), .in1(in_2[2]), .out(multiplexer_6_out), .sel(not_3_out));  // open: en
  Multiplexer multiplexer_7 (.in0(in_2[2]), .in1(in_2[1]), .out(multiplexer_7_out), .sel(not_3_out));  // open: en
  Multiplexer multiplexer_8 (.in0(in_2[1]), .in1(in_2[0]), .out(multiplexer_8_out), .sel(not_3_out));  // open: en
  Multiplexer multiplexer_9 (
    .in0(1'b0), .in1(multiplexer_1_out), .out(multiplexer_9_out), .sel(not_2_out));  // open: en
  Multiplexer multiplexer_10 (
    .in0(1'b0), .in1(multiplexer_2_out), .out(multiplexer_10_out), .sel(not_2_out));  // open: en
  Multiplexer multiplexer_11 (
    .in0(multiplexer_1_out), .in1(multiplexer_3_out), .out(multiplexer_11_out), .sel(not_2_out));  // open: en
  Multiplexer multiplexer_12 (
    .in0(multiplexer_2_out), .in1(multiplexer_4_out), .out(multiplexer_12_out), .sel(not_2_out));  // open: en
  Multiplexer multiplexer_13 (
    .in0(multiplexer_3_out), .in1(multiplexer_5_out), .out(multiplexer_13_out), .sel(not_2_out));  // open: en
  Multiplexer multiplexer_14 (
    .in0(multiplexer_4_out), .in1(multiplexer_6_out), .out(multiplexer_14_out), .sel(not_2_out));  // open: en
  Multiplexer multiplexer_15 (
    .in0(multiplexer_5_out), .in1(multiplexer_7_out), .out(multiplexer_15_out), .sel(not_2_out));  // open: en
  Multiplexer multiplexer_16 (
    .in0(multiplexer_6_out), .in1(multiplexer_8_out), .out(multiplexer_16_out), .sel(not_2_out));  // open: en
  Multiplexer multiplexer_17 (.in0(1'b0), .in1(multiplexer_9_out), .out(out_3[7]), .sel(not_1_out));  // open: en
  Multiplexer multiplexer_18 (.in0(1'b0), .in1(multiplexer_10_out), .out(out_3[6]), .sel(not_1_out));  // open: en
  Multiplexer multiplexer_19 (.in0(1'b0), .in1(multiplexer_11_out), .out(out_3[5]), .sel(not_1_out));  // open: en
  Multiplexer multiplexer_20 (.in0(1'b0), .in1(multiplexer_12_out), .out(out_3[4]), .sel(not_1_out));  // open: en
  Multiplexer multiplexer_21 (
    .in0(multiplexer_9_out), .in1(multiplexer_13_out), .out(out_3[3]), .sel(not_1_out));  // open: en
  Multiplexer multiplexer_22 (
    .in0(multiplexer_10_out), .in1(multiplexer_14_out), .out(out_3[2]), .sel(not_1_out));  // open: en
  Multiplexer multiplexer_23 (
    .in0(multiplexer_11_out), .in1(multiplexer_15_out), .out(out_3[1]), .sel(not_1_out));  // open: en
  Multiplexer multiplexer_24 (
    .in0(multiplexer_12_out), .in1(multiplexer_16_out), .out(out_3[0]), .sel(not_1_out));  // open: en
endmodule

module arifmetic_shift_right (
  input  [2:0] in_1,
  input  [7:0] in_2,
  output [7:0] out_3
);

  wire multiplexer_1_out, multiplexer_2_out, multiplexer_3_out, multiplexer_4_out, multiplexer_5_out,
       multiplexer_6_out, multiplexer_7_out, multiplexer_8_out, multiplexer_9_out, multiplexer_10_out,
       multiplexer_11_out, multiplexer_12_out, multiplexer_13_out, multiplexer_14_out, multiplexer_15_out,
       multiplexer_16_out, not_1_out, not_2_out, not_3_out;

  not not_1 (not_1_out, in_1[2]);
  not not_2 (not_2_out, in_1[1]);
  not not_3 (not_3_out, in_1[0]);
  Multiplexer multiplexer_1 (.in0(in_2[7]), .in1(in_2[7]), .out(multiplexer_1_out), .sel(not_3_out));  // open: en
  Multiplexer multiplexer_2 (.in0(in_2[7]), .in1(in_2[6]), .out(multiplexer_2_out), .sel(not_3_out));  // open: en
  Multiplexer multiplexer_3 (.in0(in_2[6]), .in1(in_2[5]), .out(multiplexer_3_out), .sel(not_3_out));  // open: en
  Multiplexer multiplexer_4 (.in0(in_2[5]), .in1(in_2[4]), .out(multiplexer_4_out), .sel(not_3_out));  // open: en
  Multiplexer multiplexer_5 (.in0(in_2[4]), .in1(in_2[3]), .out(multiplexer_5_out), .sel(not_3_out));  // open: en
  Multiplexer multiplexer_6 (.in0(in_2[3]), .in1(in_2[2]), .out(multiplexer_6_out), .sel(not_3_out));  // open: en
  Multiplexer multiplexer_7 (.in0(in_2[2]), .in1(in_2[1]), .out(multiplexer_7_out), .sel(not_3_out));  // open: en
  Multiplexer multiplexer_8 (.in0(in_2[1]), .in1(in_2[0]), .out(multiplexer_8_out), .sel(not_3_out));  // open: en
  Multiplexer multiplexer_9 (
    .in0(in_2[7]), .in1(multiplexer_1_out), .out(multiplexer_9_out), .sel(not_2_out));  // open: en
  Multiplexer multiplexer_10 (
    .in0(in_2[7]), .in1(multiplexer_2_out), .out(multiplexer_10_out), .sel(not_2_out));  // open: en
  Multiplexer multiplexer_11 (
    .in0(multiplexer_1_out), .in1(multiplexer_3_out), .out(multiplexer_11_out), .sel(not_2_out));  // open: en
  Multiplexer multiplexer_12 (
    .in0(multiplexer_2_out), .in1(multiplexer_4_out), .out(multiplexer_12_out), .sel(not_2_out));  // open: en
  Multiplexer multiplexer_13 (
    .in0(multiplexer_3_out), .in1(multiplexer_5_out), .out(multiplexer_13_out), .sel(not_2_out));  // open: en
  Multiplexer multiplexer_14 (
    .in0(multiplexer_4_out), .in1(multiplexer_6_out), .out(multiplexer_14_out), .sel(not_2_out));  // open: en
  Multiplexer multiplexer_15 (
    .in0(multiplexer_5_out), .in1(multiplexer_7_out), .out(multiplexer_15_out), .sel(not_2_out));  // open: en
  Multiplexer multiplexer_16 (
    .in0(multiplexer_6_out), .in1(multiplexer_8_out), .out(multiplexer_16_out), .sel(not_2_out));  // open: en
  Multiplexer multiplexer_17 (.in0(in_2[7]), .in1(multiplexer_9_out), .out(out_3[7]), .sel(not_1_out));  // open: en
  Multiplexer multiplexer_18 (.in0(in_2[7]), .in1(multiplexer_10_out), .out(out_3[6]), .sel(not_1_out));  // open: en
  Multiplexer multiplexer_19 (.in0(in_2[7]), .in1(multiplexer_11_out), .out(out_3[5]), .sel(not_1_out));  // open: en
  Multiplexer multiplexer_20 (.in0(in_2[7]), .in1(multiplexer_12_out), .out(out_3[4]), .sel(not_1_out));  // open: en
  Multiplexer multiplexer_21 (
    .in0(multiplexer_9_out), .in1(multiplexer_13_out), .out(out_3[3]), .sel(not_1_out));  // open: en
  Multiplexer multiplexer_22 (
    .in0(multiplexer_10_out), .in1(multiplexer_14_out), .out(out_3[2]), .sel(not_1_out));  // open: en
  Multiplexer multiplexer_23 (
    .in0(multiplexer_11_out), .in1(multiplexer_15_out), .out(out_3[1]), .sel(not_1_out));  // open: en
  Multiplexer multiplexer_24 (
    .in0(multiplexer_12_out), .in1(multiplexer_16_out), .out(out_3[0]), .sel(not_1_out));  // open: en
endmodule

module cycle_shift_left (
  input  [2:0] in_1,
  input  [7:0] in_2,
  output [7:0] out_3
);

  wire multiplexer_1_out, multiplexer_2_out, multiplexer_3_out, multiplexer_4_out, multiplexer_5_out,
       multiplexer_6_out, multiplexer_7_out, multiplexer_8_out, multiplexer_9_out, multiplexer_10_out,
       multiplexer_11_out, multiplexer_12_out, multiplexer_13_out, multiplexer_14_out, multiplexer_15_out,
       multiplexer_16_out, not_1_out, not_2_out, not_3_out;

  not not_1 (not_1_out, in_1[2]);
  not not_2 (not_2_out, in_1[1]);
  not not_3 (not_3_out, in_1[0]);
  Multiplexer multiplexer_1 (.in0(in_2[7]), .in1(in_2[0]), .out(multiplexer_1_out), .sel(not_3_out));  // open: en
  Multiplexer multiplexer_2 (.in0(in_2[0]), .in1(in_2[1]), .out(multiplexer_2_out), .sel(not_3_out));  // open: en
  Multiplexer multiplexer_3 (.in0(in_2[1]), .in1(in_2[2]), .out(multiplexer_3_out), .sel(not_3_out));  // open: en
  Multiplexer multiplexer_4 (.in0(in_2[2]), .in1(in_2[3]), .out(multiplexer_4_out), .sel(not_3_out));  // open: en
  Multiplexer multiplexer_5 (.in0(in_2[3]), .in1(in_2[4]), .out(multiplexer_5_out), .sel(not_3_out));  // open: en
  Multiplexer multiplexer_6 (.in0(in_2[4]), .in1(in_2[5]), .out(multiplexer_6_out), .sel(not_3_out));  // open: en
  Multiplexer multiplexer_7 (.in0(in_2[5]), .in1(in_2[6]), .out(multiplexer_7_out), .sel(not_3_out));  // open: en
  Multiplexer multiplexer_8 (.in0(in_2[6]), .in1(in_2[7]), .out(multiplexer_8_out), .sel(not_3_out));  // open: en
  Multiplexer multiplexer_9 (
    .in0(multiplexer_7_out), .in1(multiplexer_1_out), .out(multiplexer_9_out), .sel(not_2_out));  // open: en
  Multiplexer multiplexer_10 (
    .in0(multiplexer_8_out), .in1(multiplexer_2_out), .out(multiplexer_10_out), .sel(not_2_out));  // open: en
  Multiplexer multiplexer_11 (
    .in0(multiplexer_1_out), .in1(multiplexer_3_out), .out(multiplexer_11_out), .sel(not_2_out));  // open: en
  Multiplexer multiplexer_12 (
    .in0(multiplexer_2_out), .in1(multiplexer_4_out), .out(multiplexer_12_out), .sel(not_2_out));  // open: en
  Multiplexer multiplexer_13 (
    .in0(multiplexer_3_out), .in1(multiplexer_5_out), .out(multiplexer_13_out), .sel(not_2_out));  // open: en
  Multiplexer multiplexer_14 (
    .in0(multiplexer_4_out), .in1(multiplexer_6_out), .out(multiplexer_14_out), .sel(not_2_out));  // open: en
  Multiplexer multiplexer_15 (
    .in0(multiplexer_5_out), .in1(multiplexer_7_out), .out(multiplexer_15_out), .sel(not_2_out));  // open: en
  Multiplexer multiplexer_16 (
    .in0(multiplexer_6_out), .in1(multiplexer_8_out), .out(multiplexer_16_out), .sel(not_2_out));  // open: en
  Multiplexer multiplexer_17 (
    .in0(multiplexer_13_out), .in1(multiplexer_9_out), .out(out_3[0]), .sel(not_1_out));  // open: en
  Multiplexer multiplexer_18 (
    .in0(multiplexer_14_out), .in1(multiplexer_10_out), .out(out_3[1]), .sel(not_1_out));  // open: en
  Multiplexer multiplexer_19 (
    .in0(multiplexer_15_out), .in1(multiplexer_11_out), .out(out_3[2]), .sel(not_1_out));  // open: en
  Multiplexer multiplexer_20 (
    .in0(multiplexer_16_out), .in1(multiplexer_12_out), .out(out_3[3]), .sel(not_1_out));  // open: en
  Multiplexer multiplexer_21 (
    .in0(multiplexer_9_out), .in1(multiplexer_13_out), .out(out_3[4]), .sel(not_1_out));  // open: en
  Multiplexer multiplexer_22 (
    .in0(multiplexer_10_out), .in1(multiplexer_14_out), .out(out_3[5]), .sel(not_1_out));  // open: en
  Multiplexer multiplexer_23 (
    .in0(multiplexer_11_out), .in1(multiplexer_15_out), .out(out_3[6]), .sel(not_1_out));  // open: en
  Multiplexer multiplexer_24 (
    .in0(multiplexer_12_out), .in1(multiplexer_16_out), .out(out_3[7]), .sel(not_1_out));  // open: en
endmodule

module cycle_shift_right (
  input  [2:0] in_1,
  input  [7:0] in_2,
  output [7:0] out_3
);

  wire multiplexer_1_out, multiplexer_2_out, multiplexer_3_out, multiplexer_4_out, multiplexer_5_out,
       multiplexer_6_out, multiplexer_7_out, multiplexer_8_out, multiplexer_9_out, multiplexer_10_out,
       multiplexer_11_out, multiplexer_12_out, multiplexer_13_out, multiplexer_14_out, multiplexer_15_out,
       multiplexer_16_out, not_1_out, not_2_out, not_3_out;

  not not_1 (not_1_out, in_1[2]);
  not not_2 (not_2_out, in_1[1]);
  not not_3 (not_3_out, in_1[0]);
  Multiplexer multiplexer_1 (.in0(in_2[0]), .in1(in_2[7]), .out(multiplexer_1_out), .sel(not_3_out));  // open: en
  Multiplexer multiplexer_2 (.in0(in_2[7]), .in1(in_2[6]), .out(multiplexer_2_out), .sel(not_3_out));  // open: en
  Multiplexer multiplexer_3 (.in0(in_2[6]), .in1(in_2[5]), .out(multiplexer_3_out), .sel(not_3_out));  // open: en
  Multiplexer multiplexer_4 (.in0(in_2[5]), .in1(in_2[4]), .out(multiplexer_4_out), .sel(not_3_out));  // open: en
  Multiplexer multiplexer_5 (.in0(in_2[4]), .in1(in_2[3]), .out(multiplexer_5_out), .sel(not_3_out));  // open: en
  Multiplexer multiplexer_6 (.in0(in_2[3]), .in1(in_2[2]), .out(multiplexer_6_out), .sel(not_3_out));  // open: en
  Multiplexer multiplexer_7 (.in0(in_2[2]), .in1(in_2[1]), .out(multiplexer_7_out), .sel(not_3_out));  // open: en
  Multiplexer multiplexer_8 (.in0(in_2[1]), .in1(in_2[0]), .out(multiplexer_8_out), .sel(not_3_out));  // open: en
  Multiplexer multiplexer_9 (
    .in0(multiplexer_7_out), .in1(multiplexer_1_out), .out(multiplexer_9_out), .sel(not_2_out));  // open: en
  Multiplexer multiplexer_10 (
    .in0(multiplexer_8_out), .in1(multiplexer_2_out), .out(multiplexer_10_out), .sel(not_2_out));  // open: en
  Multiplexer multiplexer_11 (
    .in0(multiplexer_1_out), .in1(multiplexer_3_out), .out(multiplexer_11_out), .sel(not_2_out));  // open: en
  Multiplexer multiplexer_12 (
    .in0(multiplexer_2_out), .in1(multiplexer_4_out), .out(multiplexer_12_out), .sel(not_2_out));  // open: en
  Multiplexer multiplexer_13 (
    .in0(multiplexer_3_out), .in1(multiplexer_5_out), .out(multiplexer_13_out), .sel(not_2_out));  // open: en
  Multiplexer multiplexer_14 (
    .in0(multiplexer_4_out), .in1(multiplexer_6_out), .out(multiplexer_14_out), .sel(not_2_out));  // open: en
  Multiplexer multiplexer_15 (
    .in0(multiplexer_5_out), .in1(multiplexer_7_out), .out(multiplexer_15_out), .sel(not_2_out));  // open: en
  Multiplexer multiplexer_16 (
    .in0(multiplexer_6_out), .in1(multiplexer_8_out), .out(multiplexer_16_out), .sel(not_2_out));  // open: en
  Multiplexer multiplexer_17 (
    .in0(multiplexer_13_out), .in1(multiplexer_9_out), .out(out_3[0]), .sel(not_1_out));  // open: en
  Multiplexer multiplexer_18 (
    .in0(multiplexer_14_out), .in1(multiplexer_10_out), .out(out_3[7]), .sel(not_1_out));  // open: en
  Multiplexer multiplexer_19 (
    .in0(multiplexer_15_out), .in1(multiplexer_11_out), .out(out_3[6]), .sel(not_1_out));  // open: en
  Multiplexer multiplexer_20 (
    .in0(multiplexer_16_out), .in1(multiplexer_12_out), .out(out_3[5]), .sel(not_1_out));  // open: en
  Multiplexer multiplexer_21 (
    .in0(multiplexer_9_out), .in1(multiplexer_13_out), .out(out_3[4]), .sel(not_1_out));  // open: en
  Multiplexer multiplexer_22 (
    .in0(multiplexer_10_out), .in1(multiplexer_14_out), .out(out_3[3]), .sel(not_1_out));  // open: en
  Multiplexer multiplexer_23 (
    .in0(multiplexer_11_out), .in1(multiplexer_15_out), .out(out_3[2]), .sel(not_1_out));  // open: en
  Multiplexer multiplexer_24 (
    .in0(multiplexer_12_out), .in1(multiplexer_16_out), .out(out_3[1]), .sel(not_1_out));  // open: en
endmodule

module mux (
  input  in_1,
  input  in_2,
  input  in_3,
  input  in_4,
  input  [1:0] in_5,
  output out_6
);

  wire and_1_out, and_2_out, and_3_out, and_4_out, not_1_out, not_2_out, not_3_out, not_4_out;

  not not_1 (not_1_out, in_5[1]);
  not not_2 (not_2_out, in_5[0]);
  not not_3 (not_3_out, in_5[1]);
  not not_4 (not_4_out, in_5[0]);
  and and_1 (and_1_out, in_1, not_1_out, not_2_out);
  and and_2 (and_2_out, in_2, in_5[0], not_3_out);
  and and_3 (and_3_out, in_3, in_5[1], not_4_out);
  and and_4 (and_4_out, in_4, in_5[0], in_5[1]);
  or or_1 (out_6, and_1_out, and_2_out, and_3_out, and_4_out);
endmodule

module dividor (
  input  [7:0] in_1,
  input  [7:0] in_2,
  output out_3,
  output [7:0] out_4
);

  wire more_or_equal_8_bit_nosign_1_out_3, more_or_equal_8_bit_nosign_2_out_3,
       more_or_equal_8_bit_nosign_3_out_3, more_or_equal_8_bit_nosign_4_out_3,
       more_or_equal_8_bit_nosign_5_out_3, more_or_equal_8_bit_nosign_6_out_3,
       more_or_equal_8_bit_nosign_7_out_3, more_or_equal_8_bit_nosign_8_out_3,
       more_or_equal_8_bit_nosign_9_out_3, n8_bit_llogic_not_1_out_2, n8_bit_llogic_not_2_out_2,
       n8_bit_llogic_not_3_out_2, n8_bit_llogic_not_4_out_2, n8_bit_llogic_not_5_out_2,
       n8_bit_llogic_not_6_out_2, n8_bit_llogic_not_7_out_2, n8_bit_llogic_not_8_out_2,
       n8_bit_llogic_not_9_out_2;
  wire [4:4] and_4_out;
  wire [7:0] multiplier_1_cout, multiplier_1_out, multiplier_2_cout, multiplier_2_out, multiplier_3_cout,
       multiplier_3_out, multiplier_4_cout, multiplier_4_out, multiplier_5_cout, multiplier_5_out,
       multiplier_6_cout, multiplier_6_out, multiplier_7_cout, multiplier_7_out, multiplier_8_cout,
       multiplier_8_out, multiplier_9_cout, multiplier_9_out;

  Multiplier multiplier_1 (.a(in_2), .b(8'h80), .out(multiplier_1_out), .cout(multiplier_1_cout));  // open: cin
  Multiplier multiplier_2 (
    .a(in_2), .b({out_4[7], 7'b1000000}), .out(multiplier_2_out), .cout(multiplier_2_cout));  // open: cin
  Multiplier multiplier_3 (
    .a(in_2), .b({out_4[7:6], 6'b100000}), .out(multiplier_3_out), .cout(multiplier_3_cout));  // open: cin
  Multiplier multiplier_4 (
    .a(in_2), .b({out_4[7:5], 5'b10000}), .out(multiplier_4_out), .cout(multiplier_4_cout));  // open: cin
  Multiplier multiplier_5 (
    .a(in_1), .b({out_4[7:5], and_4_out[4], 4'b1000}), .out(multiplier_5_out), .cout(multiplier_5_cout));  // open: cin
  Multiplier multiplier_6 (
    .a(in_1), .b({out_4[7:4], 4'b1000}), .out(multiplier_6_out), .cout(multiplier_6_cout));  // open: cin
  more_or_equal_8_bit_nosign more_or_equal_8_bit_nosign_1 (
    .in_1(in_1), .in_2(multiplier_1_out), .out_3(more_or_equal_8_bit_nosign_1_out_3));
  _8_bit_llogic_not u_8_bit_llogic_not_1 (.in_1(multiplier_1_cout), .out_2(n8_bit_llogic_not_1_out_2));
  more_or_equal_8_bit_nosign more_or_equal_8_bit_nosign_2 (
    .in_1(in_1), .in_2(multiplier_2_out), .out_3(more_or_equal_8_bit_nosign_2_out_3));
  _8_bit_llogic_not u_8_bit_llogic_not_2 (.in_1(multiplier_2_cout), .out_2(n8_bit_llogic_not_2_out_2));
  more_or_equal_8_bit_nosign more_or_equal_8_bit_nosign_3 (
    .in_1(in_1), .in_2(multiplier_3_out), .out_3(more_or_equal_8_bit_nosign_3_out_3));
  _8_bit_llogic_not u_8_bit_llogic_not_3 (.in_1(multiplier_3_cout), .out_2(n8_bit_llogic_not_3_out_2));
  more_or_equal_8_bit_nosign more_or_equal_8_bit_nosign_4 (
    .in_1(in_1), .in_2(multiplier_4_out), .out_3(more_or_equal_8_bit_nosign_4_out_3));
  _8_bit_llogic_not u_8_bit_llogic_not_4 (.in_1(multiplier_4_cout), .out_2(n8_bit_llogic_not_4_out_2));
  more_or_equal_8_bit_nosign more_or_equal_8_bit_nosign_5 (
    .in_1(in_2), .in_2(multiplier_5_out), .out_3(more_or_equal_8_bit_nosign_5_out_3));
  _8_bit_llogic_not u_8_bit_llogic_not_5 (.in_1(multiplier_5_cout), .out_2(n8_bit_llogic_not_5_out_2));
  more_or_equal_8_bit_nosign more_or_equal_8_bit_nosign_6 (
    .in_1(in_2), .in_2(multiplier_6_out), .out_3(more_or_equal_8_bit_nosign_6_out_3));
  _8_bit_llogic_not u_8_bit_llogic_not_6 (.in_1(multiplier_6_cout), .out_2(n8_bit_llogic_not_6_out_2));
  and and_1 (out_4[7], more_or_equal_8_bit_nosign_1_out_3, n8_bit_llogic_not_1_out_2);
  and and_2 (out_4[6], more_or_equal_8_bit_nosign_2_out_3, n8_bit_llogic_not_2_out_2);
  and and_3 (out_4[5], more_or_equal_8_bit_nosign_3_out_3, n8_bit_llogic_not_3_out_2);
  and and_4 (and_4_out[4], more_or_equal_8_bit_nosign_4_out_3, n8_bit_llogic_not_4_out_2);
  and and_5 (out_4[4], more_or_equal_8_bit_nosign_5_out_3, n8_bit_llogic_not_5_out_2);
  and and_6 (out_4[3], more_or_equal_8_bit_nosign_6_out_3, n8_bit_llogic_not_6_out_2);
  Multiplier multiplier_7 (
    .a(in_2), .b({out_4[7:3], 3'b100}), .out(multiplier_7_out), .cout(multiplier_7_cout));  // open: cin
  Multiplier multiplier_8 (
    .a(in_2), .b({out_4[7:2], 2'b10}), .out(multiplier_8_out), .cout(multiplier_8_cout));  // open: cin
  Multiplier multiplier_9 (
    .a(in_2), .b({out_4[7:1], 1'b1}), .out(multiplier_9_out), .cout(multiplier_9_cout));  // open: cin
  more_or_equal_8_bit_nosign more_or_equal_8_bit_nosign_7 (
    .in_1(in_1), .in_2(multiplier_7_out), .out_3(more_or_equal_8_bit_nosign_7_out_3));
  _8_bit_llogic_not u_8_bit_llogic_not_7 (.in_1(multiplier_7_cout), .out_2(n8_bit_llogic_not_7_out_2));
  more_or_equal_8_bit_nosign more_or_equal_8_bit_nosign_8 (
    .in_1(in_1), .in_2(multiplier_8_out), .out_3(more_or_equal_8_bit_nosign_8_out_3));
  _8_bit_llogic_not u_8_bit_llogic_not_8 (.in_1(multiplier_8_cout), .out_2(n8_bit_llogic_not_8_out_2));
  more_or_equal_8_bit_nosign more_or_equal_8_bit_nosign_9 (
    .in_1(in_1), .in_2(multiplier_9_out), .out_3(more_or_equal_8_bit_nosign_9_out_3));
  _8_bit_llogic_not u_8_bit_llogic_not_9 (.in_1(multiplier_9_cout), .out_2(n8_bit_llogic_not_9_out_2));
  _8_bit_llogic_not u_8_bit_llogic_not_10 (.in_1(in_2), .out_2(out_3));
  and and_7 (out_4[2], more_or_equal_8_bit_nosign_7_out_3, n8_bit_llogic_not_7_out_2);
  and and_8 (out_4[1], more_or_equal_8_bit_nosign_8_out_3, n8_bit_llogic_not_8_out_2);
  and and_9 (out_4[0], more_or_equal_8_bit_nosign_9_out_3, n8_bit_llogic_not_9_out_2);
endmodule

module ALU (
  input  [7:0] in_1,
  input  [7:0] in_2,
  input  [2:0] in_3,
  input  [4:0] in_4,
  output [7:0] out_5,
  output out_6
);

  wire equal_8_bit_1_out_3, less_8_bit_nosign_1_out_3, less_or_equal_8_bit_nosign_1_out_3,
       more_8_bit_nosign_1_out_3, more_or_equal_8_bit_nosign_1_out_3, n8_bit_adder_1_out_4,
       n8_bit_llogic_not_1_out_2, n8_bit_logic_and_1_out_3, n8_bit_logic_or_1_out_3,
       n8_bit_logic_xor_1_out_3, n8_bit_substracter_1_out_4, not_equal_8_bit_1_out_3;
  wire [7:0] arifmetic_shift_right_1_out_3, cycle_shift_left_1_out_3, cycle_shift_right_1_out_3,
       dividor_1_out_4, logic_arifmetic_shift_left_1_out_3, logic_shift_right_1_out_3, multiplyer_1_out_3,
       multiplyer_1_out_4, n1_bit_to_8_bit_1_out_2, n1_bit_to_8_bit_2_out_2, n1_bit_to_8_bit_3_out_2,
       n1_bit_to_8_bit_4_out_2, n1_bit_to_8_bit_6_out_2, n1_bit_to_8_bit_7_out_2, n1_bit_to_8_bit_8_out_2,
       n1_bit_to_8_bit_9_out_2, n1_bit_to_8_bit_10_out_2, n8_bit_adder_1_out_3, n8_bit_and_1_out_3,
       n8_bit_or_1_out_3, n8_bit_substracter_1_out_3, n8_bit_xor_1_out_3, n8_it_not_1_out_2;

  _8_bit_and u_8_bit_and_1 (.in_1(in_1), .in_2(in_2), .out_3(n8_bit_and_1_out_3));
  _8_bit_or u_8_bit_or_1 (.in_1(in_1), .in_2(in_2), .out_3(n8_bit_or_1_out_3));
  _8_bit_xor u_8_bit_xor_1 (.in_1(in_1), .in_2(in_2), .out_3(n8_bit_xor_1_out_3));
  _8_it_not u_8_it_not_1 (.in_1(in_1), .out_2(n8_it_not_1_out_2));
  Logic_arifmetic_shift_left logic_arifmetic_shift_left_1 (
    .in_1(in_3), .in_2(in_1), .out_3(logic_arifmetic_shift_left_1_out_3));
  logic_shift_right logic_shift_right_1 (.in_1(in_3), .in_2(in_1), .out_3(logic_shift_right_1_out_3));
  arifmetic_shift_right arifmetic_shift_right_1 (.in_1(in_3), .in_2(in_1), .out_3(arifmetic_shift_right_1_out_3));
  cycle_shift_left cycle_shift_left_1 (.in_1(in_3), .in_2(in_1), .out_3(cycle_shift_left_1_out_3));
  cycle_shift_right cycle_shift_right_1 (.in_1(in_3), .in_2(in_1), .out_3(cycle_shift_right_1_out_3));
  _8_bit_adder u_8_bit_adder_1 (.in_1(in_1), .in_2(in_2), .out_3(n8_bit_adder_1_out_3), .out_4(n8_bit_adder_1_out_4));
  _8_bit_substracter u_8_bit_substracter_1 (
    .in_1(in_1), .in_2(in_2), .out_3(n8_bit_substracter_1_out_3), .out_4(n8_bit_substracter_1_out_4));
  multiplyer multiplyer_1 (.in_1(in_1), .in_2(in_2), .out_3(multiplyer_1_out_3), .out_4(multiplyer_1_out_4));
  dividor dividor_1 (.in_1(in_1), .in_2(in_2), .out_3(out_6), .out_4(dividor_1_out_4));
  _1_bit_to_8_bit u_1_bit_to_8_bit_1 (.in_1(n8_bit_logic_and_1_out_3), .out_2(n1_bit_to_8_bit_1_out_2));
  _8_bit_logic_and u_8_bit_logic_and_1 (.in_1(in_1), .in_2(in_1), .out_3(n8_bit_logic_and_1_out_3));
  _8_bit_logic_or u_8_bit_logic_or_1 (.in_1(in_1), .in_2(in_1), .out_3(n8_bit_logic_or_1_out_3));
  _1_bit_to_8_bit u_1_bit_to_8_bit_2 (.in_1(n8_bit_logic_or_1_out_3), .out_2(n1_bit_to_8_bit_2_out_2));
  _1_bit_to_8_bit u_1_bit_to_8_bit_3 (.in_1(n8_bit_logic_xor_1_out_3), .out_2(n1_bit_to_8_bit_3_out_2));
  _8_bit_logic_xor u_8_bit_logic_xor_1 (.in_1(in_1), .in_2(in_1), .out_3(n8_bit_logic_xor_1_out_3));
  _1_bit_to_8_bit u_1_bit_to_8_bit_4 (.in_1(n8_bit_llogic_not_1_out_2), .out_2(n1_bit_to_8_bit_4_out_2));
  _8_bit_llogic_not u_8_bit_llogic_not_1 (.in_1(in_1), .out_2(n8_bit_llogic_not_1_out_2));
  less_8_bit_nosign less_8_bit_nosign_1 (.in_1(in_1), .in_2(in_2), .out_3(less_8_bit_nosign_1_out_3));
  _1_bit_to_8_bit u_1_bit_to_8_bit_5 (.in_1(less_8_bit_nosign_1_out_3));  // open: out_2
  more_8_bit_nosign more_8_bit_nosign_1 (.in_1(in_1), .in_2(in_2), .out_3(more_8_bit_nosign_1_out_3));
  _1_bit_to_8_bit u_1_bit_to_8_bit_6 (.in_1(more_8_bit_nosign_1_out_3), .out_2(n1_bit_to_8_bit_6_out_2));
  equal_8_bit equal_8_bit_1 (.in_1(in_1), .in_2(in_2), .out_3(equal_8_bit_1_out_3));
  _1_bit_to_8_bit u_1_bit_to_8_bit_7 (.in_1(equal_8_bit_1_out_3), .out_2(n1_bit_to_8_bit_7_out_2));
  less_or_equal_8_bit_nosign less_or_equal_8_bit_nosign_1 (
    .in_1(in_1), .in_2(in_2), .out_3(less_or_equal_8_bit_nosign_1_out_3));
  _1_bit_to_8_bit u_1_bit_to_8_bit_8 (.in_1(less_or_equal_8_bit_nosign_1_out_3), .out_2(n1_bit_to_8_bit_8_out_2));
  more_or_equal_8_bit_nosign more_or_equal_8_bit_nosign_1 (
    .in_1(in_1), .in_2(in_2), .out_3(more_or_equal_8_bit_nosign_1_out_3));
  _1_bit_to_8_bit u_1_bit_to_8_bit_9 (.in_1(more_or_equal_8_bit_nosign_1_out_3), .out_2(n1_bit_to_8_bit_9_out_2));
  not_equal_8_bit not_equal_8_bit_1 (.in_1(in_1), .in_2(in_2), .out_3(not_equal_8_bit_1_out_3));
  _1_bit_to_8_bit u_1_bit_to_8_bit_10 (.in_1(not_equal_8_bit_1_out_3), .out_2(n1_bit_to_8_bit_10_out_2));
  Multiplexer #(.select(5), .width(8)) multiplexer_1 (
    .in0(n8_bit_and_1_out_3), .in1(n8_bit_or_1_out_3), .in2(n8_bit_xor_1_out_3), .in3(n8_it_not_1_out_2),
    .in4(logic_arifmetic_shift_left_1_out_3), .in5(logic_shift_right_1_out_3),
    .in6(arifmetic_shift_right_1_out_3), .in7(cycle_shift_left_1_out_3), .in8(cycle_shift_right_1_out_3),
    .in9(n8_bit_adder_1_out_3), .in10(n8_bit_substracter_1_out_3), .in11(multiplyer_1_out_3),
    .in12(dividor_1_out_4), .in13(n1_bit_to_8_bit_1_out_2), .in14(n1_bit_to_8_bit_2_out_2),
    .in15(n1_bit_to_8_bit_3_out_2), .in16(n1_bit_to_8_bit_4_out_2), .in17(n1_bit_to_8_bit_6_out_2),
    .in18(n1_bit_to_8_bit_7_out_2), .in19(n1_bit_to_8_bit_8_out_2), .in20(n1_bit_to_8_bit_9_out_2),
    .in21(n1_bit_to_8_bit_10_out_2), .out(out_5), .sel(in_4));  // open: in22, in23, in24, in25, in26, in27, in28, in29, in30, in31, en
endmodule

module _1_bit_to_8_bit (
  input  in_1,
  output [7:0] out_2
);


  assign out_2 = {{7{1'b0}}, in_1};
endmodule

module equal_8_bit_float (
  input  [31:0] in_1,
  input  [31:0] in_2,
  output out_3
);

  wire and_1_out, and_2_out, and_3_out, comparator_1_eq, comparator_2_eq, comparator_3_eq, comparator_4_eq,
       comparator_5_eq, comparator_6_eq, comparator_7_eq, not_1_out, not_2_out, not_3_out;

  Comparator comparator_1 (.a(in_1[30:23]), .b({8{1'b1}}), .eq(comparator_1_eq));  // open: gt, lt
  Comparator #(.width(23)) comparator_2 (.a(in_1[22:0]), .b({23{1'b0}}), .eq(comparator_2_eq));  // open: gt, lt
  Comparator comparator_3 (.a(in_2[30:23]), .b({8{1'b1}}), .eq(comparator_3_eq));  // open: gt, lt
  Comparator #(.width(23)) comparator_4 (.a(in_2[22:0]), .b({23{1'b0}}), .eq(comparator_4_eq));  // open: gt, lt
  Comparator #(.width(23)) comparator_5 (.a(in_1[22:0]), .b(in_2[22:0]), .eq(comparator_5_eq));  // open: gt, lt
  Comparator comparator_6 (.a(in_1[30:23]), .b(in_2[30:23]), .eq(comparator_6_eq));  // open: gt, lt
  Comparator #(.width(1)) comparator_7 (.a(in_1[31]), .b(in_2[31]), .eq(comparator_7_eq));  // open: gt, lt
  not not_1 (not_1_out, comparator_2_eq);
  not not_2 (not_2_out, comparator_4_eq);
  and and_1 (and_1_out, comparator_1_eq, not_1_out);
  and and_2 (and_2_out, comparator_3_eq, not_2_out);
  and and_3 (and_3_out, and_1_out, and_2_out);
  not not_3 (not_3_out, and_3_out);
  and and_4 (out_3, comparator_5_eq, comparator_6_eq, comparator_7_eq, not_3_out);
endmodule

module not_equal_8_bit_float (
  input  [31:0] in_1,
  input  [31:0] in_2,
  output out_3
);

  wire equal_8_bit_float_1_out_3;

  equal_8_bit_float equal_8_bit_float_1 (.in_1(in_1), .in_2(in_2), .out_3(equal_8_bit_float_1_out_3));
  not not_1 (out_3, equal_8_bit_float_1_out_3);
endmodule

module more_8_bit_float (
  input  [31:0] in_1,
  input  [31:0] in_2,
  output out_3
);

  wire and_1_out, and_2_out, and_3_out, and_4_out, and_5_out, comparator_1_eq, comparator_2_eq,
       comparator_3_eq, comparator_4_eq, comparator_5_eq, comparator_6_eq, comparator_7_gt, comparator_8_eq,
       comparator_8_gt, comparator_9_eq, comparator_9_lt, not_1_out, not_2_out, not_3_out,
       not_equal_8_bit_float_1_out_3, or_1_out, or_2_out, or_3_out;

  not_equal_8_bit_float not_equal_8_bit_float_1 (.in_1(in_1), .in_2(in_2), .out_3(not_equal_8_bit_float_1_out_3));
  Comparator comparator_1 (.a(in_1[30:23]), .b({8{1'b1}}), .eq(comparator_1_eq));  // open: gt, lt
  Comparator #(.width(23)) comparator_2 (.a(in_1[22:0]), .b({23{1'b0}}), .eq(comparator_2_eq));  // open: gt, lt
  Comparator comparator_3 (.a(in_1[30:23]), .b({8{1'b1}}), .eq(comparator_3_eq));  // open: gt, lt
  Comparator #(.width(23)) comparator_4 (.a(in_1[22:0]), .b({23{1'b0}}), .eq(comparator_4_eq));  // open: gt, lt
  Comparator comparator_5 (.a(in_2[30:23]), .b({8{1'b1}}), .eq(comparator_5_eq));  // open: gt, lt
  Comparator #(.width(23)) comparator_6 (.a(in_2[22:0]), .b({23{1'b0}}), .eq(comparator_6_eq));  // open: gt, lt
  and and_1 (and_1_out, not_equal_8_bit_float_1_out_3, comparator_1_eq, comparator_2_eq, in_1[31]);
  Comparator #(.width(23)) comparator_7 (.a(in_1[22:0]), .b(in_2[22:0]), .gt(comparator_7_gt));  // open: eq, lt
  Comparator comparator_8 (.a(in_1[30:23]), .b(in_2[30:23]), .gt(comparator_8_gt), .eq(comparator_8_eq));  // open: lt
  Comparator #(.width(1)) comparator_9 (
    .a(in_2[31]), .b(in_1[31]), .eq(comparator_9_eq), .lt(comparator_9_lt));  // open: gt
  not not_1 (not_1_out, comparator_4_eq);
  not not_2 (not_2_out, comparator_6_eq);
  and and_2 (and_2_out, comparator_7_gt, comparator_8_eq);
  and and_3 (and_3_out, comparator_3_eq, not_1_out);
  and and_4 (and_4_out, comparator_5_eq, not_2_out);
  or or_1 (or_1_out, and_2_out, comparator_8_gt);
  not not_3 (not_3_out, or_2_out);
  or or_2 (or_2_out, and_3_out, and_4_out);
  and and_5 (and_5_out, or_1_out, comparator_9_eq);
  or or_3 (or_3_out, and_1_out, and_5_out, comparator_9_lt);
  and and_6 (out_3, or_3_out, not_3_out);
endmodule

module less_8_bit_float (
  input  [31:0] in_1,
  input  [31:0] in_2,
  output out_3
);

  more_8_bit_float more_8_bit_float_1 (.in_1(in_2), .in_2(in_1), .out_3(out_3));
endmodule

module more_or_equal_8_bit_float (
  input  [31:0] in_1,
  input  [31:0] in_2,
  output out_3
);

  wire equal_8_bit_float_1_out_3, more_8_bit_float_1_out_3;

  equal_8_bit_float equal_8_bit_float_1 (.in_1(in_1), .in_2(in_2), .out_3(equal_8_bit_float_1_out_3));
  more_8_bit_float more_8_bit_float_1 (.in_1(in_1), .in_2(in_2), .out_3(more_8_bit_float_1_out_3));
  or or_1 (out_3, equal_8_bit_float_1_out_3, more_8_bit_float_1_out_3);
endmodule

module less_or_equal_8_bit_float (
  input  [31:0] in_1,
  input  [31:0] in_2,
  output out_3
);

  wire equal_8_bit_float_1_out_3, less_8_bit_float_1_out_3;

  equal_8_bit_float equal_8_bit_float_1 (.in_1(in_1), .in_2(in_2), .out_3(equal_8_bit_float_1_out_3));
  less_8_bit_float less_8_bit_float_1 (.in_1(in_1), .in_2(in_2), .out_3(less_8_bit_float_1_out_3));
  or or_1 (out_3, equal_8_bit_float_1_out_3, less_8_bit_float_1_out_3);
endmodule
