// Logisim project laba2.circ as structural Verilog: 14 circuits, main circuit RS-trigger
module RS_trigger (
  input  in_1,
  input  in_2,
  output out_3,
  output out_4
);

  nor nor_1 (out_3, in_1, out_4);
  nor nor_2 (out_4, out_3, in_2);
endmodule

module D_trigger (
  input  in_1,
  input  in_2,
  output out_3,
  output out_4
);

  wire and_1_out, and_2_out, not_1_out;

  and and_1 (and_1_out, in_1, not_1_out);
  not not_1 (not_1_out, in_2);
  and and_2 (and_2_out, in_1, in_2);
  RS_trigger rs_trigger_1 (.in_1(and_1_out), .in_2(and_2_out), .out_3(out_3), .out_4(out_4));
endmodule

module D_flip_flop (
  input  in_1,
  input  in_2,
  output out_3
);

  wire d_trigger_1_out_3, not_1_out;

  not not_1 (not_1_out, in_1);
  D_trigger d_trigger_1 (.in_1(not_1_out), .in_2(in_2), .out_3(d_trigger_1_out_3));  // open: out_4
  D_trigger d_trigger_2 (.in_1(in_1), .in_2(d_trigger_1_out_3), .out_3(out_3));  // open: out_4
endmodule

module Registor (
  input  in_1,
  input  in_2,
  input  [7:0] in_3,
  output [7:0] out_4
);

  wire and_1_out;

  D_flip_flop d_flip_flop_1 (.in_1(and_1_out), .in_2(in_3[0]), .out_3(out_4[0]));
  D_flip_flop d_flip_flop_2 (.in_1(and_1_out), .in_2(in_3[1]), .out_3(out_4[1]));
  D_flip_flop d_flip_flop_3 (.in_1(and_1_out), .in_2(in_3[2]), .out_3(out_4[2]));
  D_flip_flop d_flip_flop_4 (.in_1(and_1_out), .in_2(in_3[3]), .out_3(out_4[3]));
  D_flip_flop d_flip_flop_5 (.in_1(and_1_out), .in_2(in_3[4]), .out_3(out_4[4]));
  D_flip_flop d_flip_flop_6 (.in_1(and_1_out), .in_2(in_3[5]), .out_3(out_4[5]));
  D_flip_flop d_flip_flop_7 (.in_1(and_1_out), .in_2(in_3[6]), .out_3(out_4[6]));
  D_flip_flop d_flip_flop_8 (.in_1(and_1_out), .in_2(in_3[7]), .out_3(out_4[7]));
  and and_1 (and_1_out, in_2, in_1);
endmodule

module counter (
  input  in_1,
  input  [7:0] in_2,
  output [7:0] out_3
);

  wire adder_1_cout, and_1_out, clock_1_out, not_1_out, not_2_out, or_1_out;
  wire [7:0] transistor_1_out, transistor_2_out;

  not not_1 (not_1_out, in_1);
  Clock clock_1 (.out(clock_1_out));
  or or_1 (or_1_out, in_1, not_2_out);
  not not_2 (not_2_out, adder_1_cout);
  Transistor #(.width(8)) transistor_1 (.in(transistor_2_out), .out(transistor_1_out), .gate(in_1));
  Transistor #(.width(8)) transistor_2 (.in(in_2), .out(transistor_2_out), .gate(not_1_out));
  Register register_1 (.D(transistor_2_out), .Q(out_3), .clk(and_1_out));  // open: en, clr
  and and_1 (and_1_out, clock_1_out, or_1_out);
  Adder adder_1 (.a(8'h1), .b(out_3), .out(transistor_1_out), .cout(adder_1_cout));  // open: cin
endmodule

module ALU (
  input  [15:0] in_1,
  input  [15:0] in_2,
  input  [3:0] in_3,
  output [15:0] out_4
);

  wire clock_1_out, locker_1_out_4, locker_1_out_5, locker_1_out_6, locker_1_out_7;
  wire [1:0] picker_1_out_2;
  wire [15:0] adder_1_out, and_1_out, demultiplexer_1_out0, demultiplexer_1_out1, demultiplexer_1_out2,
       demultiplexer_2_out1, demultiplexer_2_out2, divider_1_out, divider_2_rem, mem2reg_1_out_3,
       mem2reg_1_out_4, mem2reg_1_out_5, mem2reg_1_out_6, mem2reg_2_out_3, mem2reg_2_out_4, mem2reg_2_out_5,
       mem2reg_2_out_6, multiplexer_1_out, multiplexer_2_out, multiplexer_3_out, multiplexer_4_out,
       multiplexer_5_out, multiplier_1_out, not_1_out, not_2_out_2, or_1_out, reg2mem_1_out_6,
       reg2mem_2_out_6, reg2reg_1_out_7, reg2reg_1_out_8, reg2reg_1_out_9, reg2reg_1_out_10, reg_1_out,
       reg_2_out, reg_3_out, reg_4_out, shl_1_out_3, shr_1_out_3, subtractor_1_out, xor_1_out;

  Demultiplexer #(.select(4), .width(16)) demultiplexer_1 (
    .out0(demultiplexer_1_out0), .out1(demultiplexer_1_out1), .out2(demultiplexer_1_out2), .in(in_1),
    .sel(in_3));  // open: out3, out4, out5, out6, out7, out8, out9, out10, out11, out12, out13, out14, out15, en
  Demultiplexer #(.select(4), .width(16)) demultiplexer_2 (
    .out1(demultiplexer_2_out1), .out2(demultiplexer_2_out2), .in(in_2), .sel(in_3));  // open: out0, out3, out4, out5, out6, out7, out8, out9, out10, out11, out12, out13, out14, out15, en
  reg2reg reg2reg_1 (
    .in_1(demultiplexer_1_out2), .in_2(demultiplexer_2_out2), .in_3(reg_1_out), .in_4(reg_2_out),
    .in_5(reg_3_out), .in_6(reg_4_out), .out_7(reg2reg_1_out_7), .out_8(reg2reg_1_out_8),
    .out_9(reg2reg_1_out_9), .out_10(reg2reg_1_out_10));
  reg2mem reg2mem_1 (
    .in_1(in_1), .in_2(reg_1_out), .in_3(reg_2_out), .in_4(reg_3_out), .in_5(reg_4_out),
    .out_6(reg2mem_1_out_6));
  reg2mem reg2mem_2 (
    .in_1(in_2), .in_2(reg_1_out), .in_3(reg_2_out), .in_4(reg_3_out), .in_5(reg_4_out),
    .out_6(reg2mem_2_out_6));
  mem2reg mem2reg_1 (
    .in_1(demultiplexer_1_out1), .in_2(demultiplexer_2_out1), .out_3(mem2reg_1_out_3),
    .out_4(mem2reg_1_out_4), .out_5(mem2reg_1_out_5), .out_6(mem2reg_1_out_6));
  picker picker_1 (.in_1(in_3), .out_2(picker_1_out_2));
  Multiplexer #(.select(2), .width(16)) multiplexer_1 (
    .in0(mem2reg_1_out_3), .in1(reg2reg_1_out_7), .in2(mem2reg_2_out_3), .out(multiplexer_1_out),
    .sel(picker_1_out_2));  // open: in3, en
  Multiplexer #(.select(2), .width(16)) multiplexer_2 (
    .in0(mem2reg_1_out_4), .in1(reg2reg_1_out_8), .in2(mem2reg_2_out_4), .out(multiplexer_2_out),
    .sel(picker_1_out_2));  // open: in3, en
  Multiplexer #(.select(2), .width(16)) multiplexer_3 (
    .in0(mem2reg_1_out_5), .in1(reg2reg_1_out_9), .in2(mem2reg_2_out_5), .out(multiplexer_3_out),
    .sel(picker_1_out_2));  // open: in3, en
  Multiplexer #(.select(2), .width(16)) multiplexer_4 (
    .in0(mem2reg_1_out_6), .in1(reg2reg_1_out_10), .in2(mem2reg_2_out_6), .out(multiplexer_4_out),
    .sel(picker_1_out_2));  // open: in3, en
  Clock clock_1 (.out(clock_1_out));
  Register #(.width(16)) register_1 (
    .D(multiplexer_1_out), .en(locker_1_out_4), .Q(reg_1_out), .clk(clock_1_out));  // open: clr
  Register #(.width(16)) register_2 (
    .D(multiplexer_2_out), .en(locker_1_out_5), .Q(reg_2_out), .clk(clock_1_out));  // open: clr
  Register #(.width(16)) register_3 (
    .D(multiplexer_3_out), .en(locker_1_out_6), .Q(reg_3_out), .clk(clock_1_out));  // open: clr
  Register #(.width(16)) register_4 (
    .D(multiplexer_4_out), .en(locker_1_out_7), .Q(reg_4_out), .clk(clock_1_out));  // open: clr
  Adder #(.width(16)) adder_1 (.a(reg2mem_1_out_6), .b(reg2mem_2_out_6), .out(adder_1_out));  // open: cin, cout
  Subtractor #(.width(16)) subtractor_1 (
    .a(reg2mem_1_out_6), .b(reg2mem_2_out_6), .out(subtractor_1_out));  // open: bin, bout
  Multiplier #(.width(16)) multiplier_1 (
    .a(reg2mem_1_out_6), .b(reg2mem_2_out_6), .out(multiplier_1_out));  // open: cin, cout
  Divider #(.width(16)) divider_1 (.a(reg2mem_1_out_6), .b(reg2mem_1_out_6), .out(divider_1_out));  // open: upper, rem
  Divider #(.width(16)) divider_2 (.a(reg2mem_1_out_6), .b(reg2mem_2_out_6), .rem(divider_2_rem));  // open: out, upper
  shl shl_1 (.in_1(reg2mem_1_out_6), .in_2(reg2mem_2_out_6), .out_3(shl_1_out_3));
  shr shr_1 (.in_1(reg2mem_1_out_6), .in_2(reg2mem_2_out_6), .out_3(shr_1_out_3));
  assign and_1_out = reg2mem_1_out_6 & reg2mem_2_out_6;  // AND_Gate and_1, 16 bits wide
  assign xor_1_out = reg2mem_1_out_6 ^ reg2mem_2_out_6;  // XOR_Gate xor_1, 16 bits wide
  assign or_1_out = reg2mem_1_out_6 | reg2mem_2_out_6;  // OR_Gate or_1, 16 bits wide
  assign not_1_out = ~reg2mem_1_out_6;  // NOT_Gate not_1, 16 bits wide
  \not  not_2 (.in_1(reg2mem_1_out_6), .out_2(not_2_out_2));
  locker locker_1 (
    .in_1(in_1), .in_2(in_2), .in_3(in_3), .out_4(locker_1_out_4), .out_5(locker_1_out_5),
    .out_6(locker_1_out_6), .out_7(locker_1_out_7));
  Multiplexer #(.select(4), .width(16)) multiplexer_5 (
    .in0({16{1'b0}}), .in1({16{1'b0}}), .in2({16{1'b0}}), .in3(adder_1_out), .in4(subtractor_1_out),
    .in5(multiplier_1_out), .in6(divider_1_out), .in7(divider_2_rem), .in8(shl_1_out_3), .in9(shr_1_out_3),
    .in10(and_1_out), .in11(xor_1_out), .in12(or_1_out), .in13(not_1_out), .in14(not_2_out_2),
    .out(multiplexer_5_out), .sel(in_3));  // open: in15, en
  mem2reg mem2reg_2 (
    .in_1(multiplexer_5_out), .in_2(in_1), .out_3(mem2reg_2_out_3), .out_4(mem2reg_2_out_4),
    .out_5(mem2reg_2_out_5), .out_6(mem2reg_2_out_6));
  reg2mem reg2mem_3 (
    .in_1(demultiplexer_1_out0), .in_2(reg_1_out), .in_3(reg_2_out), .in_4(reg_3_out), .in_5(reg_4_out),
    .out_6(out_4));

  // Other names for the same wires on the sheet: control[3:0] = in_3; v1[15:0] = in_1; v2[15:0] = in_2

  // Notes on the sheet:
  //   0 - reg2mem
  //   1 - mem2reg
  //   2 - reg2reg
  //   3 - sum
  //   4 - sub
  //   5 - mul
  //   6 - div
  //   7 - mod
  //   8 - shl
  //   9 - shr
  //   10 - and
  //   11 - xor
  //   12 - or
  //   13 - inv
  //   14 - not
endmodule

module mem2reg (
  input  [15:0] in_1,
  input  [15:0] in_2,
  output [15:0] out_3,
  output [15:0] out_4,
  output [15:0] out_5,
  output [15:0] out_6
);

  Demultiplexer #(.select(2), .width(16)) demultiplexer_1 (
    .out0(out_3), .out1(out_4), .out2(out_5), .out3(out_6), .in(in_1), .sel(in_2[1:0]));  // open: en
endmodule

module reg2mem (
  input  [15:0] in_1,
  input  [15:0] in_2,
  input  [15:0] in_3,
  input  [15:0] in_4,
  input  [15:0] in_5,
  output [15:0] out_6
);

  Multiplexer #(.select(2), .width(16)) multiplexer_1 (
    .in0(in_2), .in1(in_3), .in2(in_4), .in3(in_5), .out(out_6), .sel(in_1[1:0]));  // open: en
endmodule

module reg2reg (
  input  [15:0] in_1,
  input  [15:0] in_2,
  input  [15:0] in_3,
  input  [15:0] in_4,
  input  [15:0] in_5,
  input  [15:0] in_6,
  output [15:0] out_7,
  output [15:0] out_8,
  output [15:0] out_9,
  output [15:0] out_10
);

  wire [15:0] multiplexer_1_out;

  Multiplexer #(.select(2), .width(16)) multiplexer_1 (
    .in0(in_3), .in1(in_4), .in2(in_5), .in3(in_6), .out(multiplexer_1_out), .sel(in_1[1:0]));  // open: en
  Demultiplexer #(.select(2), .width(16)) demultiplexer_1 (
    .out0(out_7), .out1(out_8), .out2(out_9), .out3(out_10), .in(multiplexer_1_out), .sel(in_2[1:0]));  // open: en
endmodule

module locker (
  input  [15:0] in_1,
  input  [15:0] in_2,
  input  [3:0] in_3,
  output out_4,
  output out_5,
  output out_6,
  output out_7
);

  wire and_1_out, and_2_out, and_3_out, and_4_out, and_5_out, and_6_out, and_7_out, and_8_out,
       comparator_1_gt, comparator_2_eq, comparator_3_eq, not_1_out, not_2_out, not_3_out, not_4_out,
       not_5_out, not_6_out, not_7_out, not_8_out, or_1_out;

  Comparator #(.width(4)) comparator_1 (.a(in_3), .b(4'b0010), .gt(comparator_1_gt));  // open: eq, lt
  Comparator #(.width(4)) comparator_2 (.a(in_3), .b(4'b0010), .eq(comparator_2_eq));  // open: gt, lt
  Comparator #(.width(4)) comparator_3 (.a(in_3), .b(4'b0001), .eq(comparator_3_eq));  // open: gt, lt
  or or_1 (or_1_out, comparator_2_eq, comparator_3_eq);
  not not_1 (not_1_out, in_1[0]);
  not not_2 (not_2_out, in_1[1]);
  not not_3 (not_3_out, in_1[1]);
  not not_4 (not_4_out, in_1[0]);
  not not_5 (not_5_out, in_2[0]);
  not not_6 (not_6_out, in_2[1]);
  not not_7 (not_7_out, in_2[1]);
  not not_8 (not_8_out, in_2[0]);
  and and_1 (and_1_out, not_1_out, not_2_out, comparator_1_gt);
  and and_2 (and_2_out, in_1[0], not_3_out, comparator_1_gt);
  and and_3 (and_3_out, not_4_out, in_1[1], comparator_1_gt);
  and and_4 (and_4_out, in_1[0], in_1[1], comparator_1_gt);
  and and_5 (and_5_out, not_5_out, not_6_out, or_1_out);
  and and_6 (and_6_out, in_2[0], not_7_out, or_1_out);
  and and_7 (and_7_out, not_8_out, in_2[1], or_1_out);
  and and_8 (and_8_out, in_2[0], in_2[1], or_1_out);
  or or_2 (out_4, and_1_out, and_5_out);
  or or_3 (out_5, and_2_out, and_6_out);
  or or_4 (out_6, and_3_out, and_7_out);
  or or_5 (out_7, and_4_out, and_8_out);
endmodule

module picker (
  input  [3:0] in_1,
  output [1:0] out_2
);

  Multiplexer #(.select(4), .width(2)) multiplexer_1 (
    .in0(2'b00), .in1(2'b00), .in2(2'b01), .in3(2'b10), .in4(2'b10), .in5(2'b10), .in6(2'b10), .in7(2'b10),
    .in8(2'b10), .in9(2'b10), .in10(2'b10), .in11(2'b10), .in12(2'b10), .in13(2'b10), .in14(2'b10),
    .in15(2'b10), .out(out_2), .sel(in_1));  // open: en
endmodule

module shl (
  input  [15:0] in_1,
  input  [15:0] in_2,
  output [15:0] out_3
);

  Shifter #(.width(16)) shifter_1 (.in(in_1), .\dist (in_2[3:0]), .out(out_3));
endmodule

module shr (
  input  [15:0] in_1,
  input  [15:0] in_2,
  output [15:0] out_3
);

  Shifter #(.width(16), .shift("lr")) shifter_1 (.in(in_1), .\dist (in_2[3:0]), .out(out_3));
endmodule

module \not  (
  input  [15:0] in_1,
  output [15:0] out_2
);

  nor nor_1 (out_2[0], in_1[0], in_1[1], in_1[2], in_1[3], in_1[4], in_1[5], in_1[6], in_1[7], in_1[8], in_1[9], in_1[10], in_1[11], in_1[12], in_1[13], in_1[14], in_1[15]);

  assign out_2[15:1] = {15{1'b0}};
endmodule
